// Logisim project BCD To 7 Segments.circ as structural Verilog
module BCD_To_7_Segments (
  input  A,
  input  B,
  input  C,
  input  D,
  output out_5,
  output out_6,
  output c_2,
  output out_8,
  output e,
  output f,
  output out_11
);

  wire and_1_out, and_2_out, and_3_out, and_4_out, and_5_out, and_6_out, and_7_out, and_8_out, and_9_out,
       and_10_out, not_2_out, not_3_out, not_4_out;

  // NOT_Gate not_1 has open pins: in=A, out=open
  not not_2 (not_2_out, B);
  not not_3 (not_3_out, C);
  not not_4 (not_4_out, D);
  and and_1 (and_1_out, not_2_out, not_4_out);
  and and_2 (and_2_out, B, D);
  and and_3 (and_3_out, C, D);
  and and_4 (and_4_out, not_3_out, not_4_out);
  and and_5 (and_5_out, C, not_4_out);
  and and_6 (and_6_out, not_2_out, C);
  and and_7 (and_7_out, B, D, not_3_out);
  and and_8 (and_8_out, A, not_3_out);
  and and_9 (and_9_out, B, not_3_out);
  and and_10 (and_10_out, B, not_4_out);
  or or_1 (out_5, C, A, and_1_out, and_2_out);
  or or_2 (out_6, A, not_2_out, and_3_out, and_4_out);
  or or_3 (c_2, B, D, not_3_out);
  or or_4 (out_8, A, and_1_out, and_5_out, and_6_out, and_7_out);
  or or_5 (e, and_5_out, and_1_out);
  or or_6 (f, and_4_out, and_8_out, and_9_out, and_10_out);
  or or_7 (out_11, and_5_out, and_6_out, and_9_out, and_8_out);

  // Notes on the sheet:
  //   a
  //   b
  //   d
  //   g
endmodule
