// Logisim project Binary_To_BCD(8-Bits).circ as structural Verilog
module Binary_To_BCD_4_Bits (
  input  A3,
  input  A2,
  input  A1,
  input  A0,
  output S3,
  output S2,
  output S1,
  output S0
);

  wire A1A0_out, A1A2_out, A2A0_out, A2A1_A0_out, A2A1_out, A2A1A0_out, A3_A2_A0_out, A3A0_2_out, A3A0_out,
       not_1_out, not_2_out, not_3_out, not_4_out;

  not not_1 (not_1_out, A2);
  not not_2 (not_2_out, A1);
  not not_3 (not_3_out, A0);
  not not_4 (not_4_out, A3);
  and A2A0 (A2A0_out, A2, A0);
  and A2A1 (A2A1_out, A2, A1);
  and A3A0 (A3A0_out, A3, A0);
  and A2A1_A0 (A2A1_A0_out, A2, not_2_out, not_3_out);
  and A1A0 (A1A0_out, A1, A0);
  and A1A2 (A1A2_out, A1, not_1_out);
  and A3A0_2 (A3A0_2_out, A3, not_3_out);
  and A3_A2_A0 (A3_A2_A0_out, not_4_out, not_1_out, A0);
  and A2A1A0 (A2A1A0_out, A2, A1, not_3_out);
  or or_1 (S3, A3, A2A0_out, A2A1_out);
  or or_2 (S2, A3A0_out, A2A1_A0_out);
  or or_3 (S1, A1A0_out, A1A2_out, A3A0_2_out);
  or or_4 (S0, A3A0_2_out, A3_A2_A0_out, A2A1A0_out);
endmodule

module Binary_To_BCD_8_Bits (
  input  A7,
  input  A6,
  input  A5,
  input  A4,
  input  A3,
  input  A2,
  input  A1,
  input  A0,
  output out_9,
  output out_10,
  output out_11,
  output out_12,
  output out_13,
  output out_14,
  output out_15,
  output out_16,
  output out_17,
  output out_18,
  output out_19,
  output out_20
);

  wire binary_to_bcd_4_bits_1_s0, binary_to_bcd_4_bits_1_s1, binary_to_bcd_4_bits_1_s2, C1_s0, C1_s1, C1_s2,
       C1_s3, C2_s0, C2_s1, C2_s2, C2_s3, C3_s0, C3_s1, C3_s2, C3_s3, C4_s0, C4_s1, C4_s2, C4_s3;

  Binary_To_BCD_4_Bits C1 (.A3(1'b0), .A2(A7), .A1(A6), .A0(A5), .S3(C1_s3), .S2(C1_s2), .S1(C1_s1), .S0(C1_s0));
  Binary_To_BCD_4_Bits C2 (.A3(C1_s2), .A2(C1_s1), .A1(C1_s0), .A0(A4), .S3(C2_s3), .S2(C2_s2), .S1(C2_s1), .S0(C2_s0));
  Binary_To_BCD_4_Bits C3 (.A3(C2_s2), .A2(C2_s1), .A1(C2_s0), .A0(A3), .S3(C3_s3), .S2(C3_s2), .S1(C3_s1), .S0(C3_s0));
  Binary_To_BCD_4_Bits C4 (.A3(C3_s2), .A2(C3_s1), .A1(C3_s0), .A0(A2), .S3(C4_s3), .S2(C4_s2), .S1(C4_s1), .S0(C4_s0));
  Binary_To_BCD_4_Bits C5 (
    .A3(C4_s2), .A2(C4_s1), .A1(C4_s0), .A0(A1), .S3(out_16), .S2(out_17), .S1(out_18), .S0(out_19));
  Binary_To_BCD_4_Bits binary_to_bcd_4_bits_1 (
    .A3(1'b0), .A2(C1_s3), .A1(C2_s3), .A0(C3_s3), .S3(out_11), .S2(binary_to_bcd_4_bits_1_s2),
    .S1(binary_to_bcd_4_bits_1_s1), .S0(binary_to_bcd_4_bits_1_s0));
  Binary_To_BCD_4_Bits binary_to_bcd_4_bits_2 (
    .A3(binary_to_bcd_4_bits_1_s2), .A2(binary_to_bcd_4_bits_1_s1), .A1(binary_to_bcd_4_bits_1_s0),
    .A0(C4_s3), .S3(out_12), .S2(out_13), .S1(out_14), .S0(out_15));

  assign out_9 = 1'b0;
  assign out_10 = 1'b0;
  assign out_20 = A0;

  // Notes on the sheet:
  //   Ground(0)
  //   Last Two Pins (Always (0)) Just because we need 12 Output Bit 
  //   K4
  //   K3
  //   K2
  //   K1
  //   V4
  //   V3
  //   V2
  //   V1
  //   W4
  //   W3
  //   W2
  //   W1
  //   S4
  //   S3
  //   S2
  //   S1
  //   P4
  //   P3
  //   P2
  //   P1
  //   P0
  //   P9
  //   P8
  //   P7
  //   P6
  //   P5
endmodule

module BCD_To_7_Segments (
  input  A,
  input  B,
  input  C,
  input  D,
  output out_5,
  output out_6,
  output c_2,
  output out_8,
  output e,
  output f,
  output out_11
);

  wire and_1_out, and_2_out, and_3_out, and_4_out, and_5_out, and_6_out, and_7_out, and_8_out, and_9_out,
       and_10_out, not_2_out, not_3_out, not_4_out;

  // NOT_Gate not_1 has open pins: in=A, out=open
  not not_2 (not_2_out, B);
  not not_3 (not_3_out, C);
  not not_4 (not_4_out, D);
  and and_1 (and_1_out, not_2_out, not_4_out);
  and and_2 (and_2_out, B, D);
  and and_3 (and_3_out, C, D);
  and and_4 (and_4_out, not_3_out, not_4_out);
  and and_5 (and_5_out, C, not_4_out);
  and and_6 (and_6_out, not_2_out, C);
  and and_7 (and_7_out, B, D, not_3_out);
  and and_8 (and_8_out, A, not_3_out);
  and and_9 (and_9_out, B, not_3_out);
  and and_10 (and_10_out, B, not_4_out);
  or or_1 (out_5, C, A, and_1_out, and_2_out);
  or or_2 (out_6, A, not_2_out, and_3_out, and_4_out);
  or or_3 (c_2, B, D, not_3_out);
  or or_4 (out_8, A, and_1_out, and_5_out, and_6_out, and_7_out);
  or or_5 (e, and_5_out, and_1_out);
  or or_6 (f, and_4_out, and_8_out, and_9_out, and_10_out);
  or or_7 (out_11, and_5_out, and_6_out, and_9_out, and_8_out);

  // Notes on the sheet:
  //   a
  //   b
  //   d
  //   g
endmodule

module FULL (
  input  A7,
  input  A6,
  input  A5,
  input  A4,
  input  A3,
  input  A2,
  input  A1,
  input  A0
);

  wire bcd_to_7_segments_1_c_2, bcd_to_7_segments_1_e, bcd_to_7_segments_1_f, bcd_to_7_segments_1_out_5,
       bcd_to_7_segments_1_out_6, bcd_to_7_segments_1_out_8, bcd_to_7_segments_1_out_11,
       bcd_to_7_segments_2_c_2, bcd_to_7_segments_2_e, bcd_to_7_segments_2_f, bcd_to_7_segments_2_out_5,
       bcd_to_7_segments_2_out_6, bcd_to_7_segments_2_out_8, bcd_to_7_segments_2_out_11,
       bcd_to_7_segments_3_c_2, bcd_to_7_segments_3_e, bcd_to_7_segments_3_f, bcd_to_7_segments_3_out_5,
       bcd_to_7_segments_3_out_6, bcd_to_7_segments_3_out_8, bcd_to_7_segments_3_out_11,
       binary_to_bcd_8_bits_1_out_9, binary_to_bcd_8_bits_1_out_10, binary_to_bcd_8_bits_1_out_11,
       binary_to_bcd_8_bits_1_out_12, binary_to_bcd_8_bits_1_out_13, binary_to_bcd_8_bits_1_out_14,
       binary_to_bcd_8_bits_1_out_15, binary_to_bcd_8_bits_1_out_16, binary_to_bcd_8_bits_1_out_17,
       binary_to_bcd_8_bits_1_out_18, binary_to_bcd_8_bits_1_out_19, binary_to_bcd_8_bits_1_out_20;

  Binary_To_BCD_8_Bits binary_to_bcd_8_bits_1 (
    .A7(A7), .A6(A6), .A5(A5), .A4(A4), .A3(A3), .A2(A2), .A1(A1), .A0(A0),
    .out_9(binary_to_bcd_8_bits_1_out_9), .out_10(binary_to_bcd_8_bits_1_out_10),
    .out_11(binary_to_bcd_8_bits_1_out_11), .out_12(binary_to_bcd_8_bits_1_out_12),
    .out_13(binary_to_bcd_8_bits_1_out_13), .out_14(binary_to_bcd_8_bits_1_out_14),
    .out_15(binary_to_bcd_8_bits_1_out_15), .out_16(binary_to_bcd_8_bits_1_out_16),
    .out_17(binary_to_bcd_8_bits_1_out_17), .out_18(binary_to_bcd_8_bits_1_out_18),
    .out_19(binary_to_bcd_8_bits_1_out_19), .out_20(binary_to_bcd_8_bits_1_out_20));
  BCD_To_7_Segments bcd_to_7_segments_1 (
    .A(binary_to_bcd_8_bits_1_out_9), .B(binary_to_bcd_8_bits_1_out_10), .C(binary_to_bcd_8_bits_1_out_11),
    .D(binary_to_bcd_8_bits_1_out_12), .out_5(bcd_to_7_segments_1_out_5), .out_6(bcd_to_7_segments_1_out_6),
    .c_2(bcd_to_7_segments_1_c_2), .out_8(bcd_to_7_segments_1_out_8), .e(bcd_to_7_segments_1_e),
    .f(bcd_to_7_segments_1_f), .out_11(bcd_to_7_segments_1_out_11));
  BCD_To_7_Segments bcd_to_7_segments_2 (
    .A(binary_to_bcd_8_bits_1_out_13), .B(binary_to_bcd_8_bits_1_out_14), .C(binary_to_bcd_8_bits_1_out_15),
    .D(binary_to_bcd_8_bits_1_out_16), .out_5(bcd_to_7_segments_2_out_5), .out_6(bcd_to_7_segments_2_out_6),
    .c_2(bcd_to_7_segments_2_c_2), .out_8(bcd_to_7_segments_2_out_8), .e(bcd_to_7_segments_2_e),
    .f(bcd_to_7_segments_2_f), .out_11(bcd_to_7_segments_2_out_11));
  BCD_To_7_Segments bcd_to_7_segments_3 (
    .A(binary_to_bcd_8_bits_1_out_17), .B(binary_to_bcd_8_bits_1_out_18), .C(binary_to_bcd_8_bits_1_out_19),
    .D(binary_to_bcd_8_bits_1_out_20), .out_5(bcd_to_7_segments_3_out_5), .out_6(bcd_to_7_segments_3_out_6),
    .c_2(bcd_to_7_segments_3_c_2), .out_8(bcd_to_7_segments_3_out_8), .e(bcd_to_7_segments_3_e),
    .f(bcd_to_7_segments_3_f), .out_11(bcd_to_7_segments_3_out_11));
  _7_Segment_Display u_7_segment_display_1 (
    .g(bcd_to_7_segments_1_out_11), .f(bcd_to_7_segments_1_f), .a(bcd_to_7_segments_1_out_5),
    .b(bcd_to_7_segments_1_out_6), .e(bcd_to_7_segments_1_e), .d(bcd_to_7_segments_1_out_8),
    .c(bcd_to_7_segments_1_c_2));  // open: dp
  _7_Segment_Display u_7_segment_display_2 (
    .g(bcd_to_7_segments_2_out_11), .f(bcd_to_7_segments_2_f), .a(bcd_to_7_segments_2_out_5),
    .b(bcd_to_7_segments_2_out_6), .e(bcd_to_7_segments_2_e), .d(bcd_to_7_segments_2_out_8),
    .c(bcd_to_7_segments_2_c_2));  // open: dp
  _7_Segment_Display u_7_segment_display_3 (
    .g(bcd_to_7_segments_3_out_11), .f(bcd_to_7_segments_3_f), .a(bcd_to_7_segments_3_out_5),
    .b(bcd_to_7_segments_3_out_6), .e(bcd_to_7_segments_3_e), .d(bcd_to_7_segments_3_out_8),
    .c(bcd_to_7_segments_3_c_2));  // open: dp
endmodule
