// Logisim project Division.circ as structural Verilog
module _4_Bit_Sub (
  input  A0,
  input  B0,
  input  A1,
  input  B1,
  input  A2,
  input  B2,
  input  A3,
  input  B3,
  input  CP,
  output out_10,
  output out_11,
  output out_12,
  output out_13,
  output out_14
);

  wire full_subtractor_1_c, full_subtractor_2_c, full_subtractor_3_c;

  Full_Subtractor full_subtractor_1 (.A(A0), .B(B0), .cp(CP), .S(out_10), .C(full_subtractor_1_c));
  Full_Subtractor full_subtractor_2 (.A(A1), .B(B1), .cp(full_subtractor_1_c), .S(out_11), .C(full_subtractor_2_c));
  Full_Subtractor full_subtractor_3 (.A(A2), .B(B2), .cp(full_subtractor_2_c), .S(out_12), .C(full_subtractor_3_c));
  Full_Subtractor full_subtractor_4 (.A(A3), .B(B3), .cp(full_subtractor_3_c), .S(out_13), .C(out_14));
endmodule

module Full_Subtractor (
  input  A,
  input  B,
  input  cp,
  output S,
  output C
);

  wire and_1_out, and_2_out, and_3_out, not_1_out;

  not not_1 (not_1_out, A);
  xor xor_1 (S, A, B, cp);
  and and_1 (and_1_out, not_1_out, B);
  and and_2 (and_2_out, not_1_out, cp);
  and and_3 (and_3_out, B, cp);
  or or_1 (C, and_1_out, and_2_out, and_3_out);
endmodule

module Full_Division_With_Sign (
  input  A3,
  input  A2,
  input  A1,
  input  A0,
  input  B3,
  input  B2,
  input  B1,
  input  B0,
  input  A_SIGN,
  input  B_SIGN,
  output Q0,
  output Q1,
  output Q2,
  output Q3,
  output SIGN
);

  wire multiplexer_1_out, multiplexer_2_out, multiplexer_3_out, multiplexer_4_out, multiplexer_5_out,
       multiplexer_6_out, multiplexer_7_out, multiplexer_8_out, multiplexer_9_out, n4_bit_sub_1_out_10,
       n4_bit_sub_1_out_11, n4_bit_sub_1_out_12, n4_bit_sub_1_out_13, n4_bit_sub_1_out_14,
       n4_bit_sub_2_out_10, n4_bit_sub_2_out_11, n4_bit_sub_2_out_12, n4_bit_sub_2_out_14,
       n4_bit_sub_3_out_10, n4_bit_sub_3_out_11, n4_bit_sub_3_out_12, n4_bit_sub_3_out_14,
       n4_bit_sub_4_out_14;

  _4_Bit_Sub u_4_bit_sub_1 (
    .A0(A3), .B0(B0), .A1(1'b0), .B1(B1), .A2(1'b0), .B2(B2), .A3(1'b0), .B3(B3), .CP(1'b0),
    .out_10(n4_bit_sub_1_out_10), .out_11(n4_bit_sub_1_out_11), .out_12(n4_bit_sub_1_out_12),
    .out_13(n4_bit_sub_1_out_13), .out_14(n4_bit_sub_1_out_14));
  Multiplexer #(.enable("false")) multiplexer_1 (
    .in0(n4_bit_sub_1_out_10), .in1(A3), .out(multiplexer_1_out), .sel(n4_bit_sub_1_out_14));
  Multiplexer #(.enable("false")) multiplexer_2 (
    .in0(n4_bit_sub_1_out_11), .in1(1'b0), .out(multiplexer_2_out), .sel(n4_bit_sub_1_out_14));
  Multiplexer #(.enable("false")) multiplexer_3 (
    .in0(n4_bit_sub_1_out_12), .in1(1'b0), .out(multiplexer_3_out), .sel(n4_bit_sub_1_out_14));
  _4_Bit_Sub u_4_bit_sub_2 (
    .A0(A2), .B0(B0), .A1(multiplexer_1_out), .B1(B1), .A2(multiplexer_2_out), .B2(B2),
    .A3(multiplexer_3_out), .B3(B3), .CP(1'b0), .out_10(n4_bit_sub_2_out_10), .out_11(n4_bit_sub_2_out_11),
    .out_12(n4_bit_sub_2_out_12), .out_13(n4_bit_sub_1_out_13), .out_14(n4_bit_sub_2_out_14));
  Multiplexer #(.enable("false")) multiplexer_4 (
    .in0(n4_bit_sub_2_out_10), .in1(A2), .out(multiplexer_4_out), .sel(n4_bit_sub_2_out_14));
  Multiplexer #(.enable("false")) multiplexer_5 (
    .in0(n4_bit_sub_2_out_11), .in1(multiplexer_1_out), .out(multiplexer_5_out), .sel(n4_bit_sub_2_out_14));
  Multiplexer #(.enable("false")) multiplexer_6 (
    .in0(n4_bit_sub_2_out_12), .in1(multiplexer_2_out), .out(multiplexer_6_out), .sel(n4_bit_sub_2_out_14));
  _4_Bit_Sub u_4_bit_sub_3 (
    .A0(A1), .B0(B0), .A1(multiplexer_4_out), .B1(B1), .A2(multiplexer_5_out), .B2(B2),
    .A3(multiplexer_6_out), .B3(B3), .CP(1'b0), .out_10(n4_bit_sub_3_out_10), .out_11(n4_bit_sub_3_out_11),
    .out_12(n4_bit_sub_3_out_12), .out_13(n4_bit_sub_1_out_13), .out_14(n4_bit_sub_3_out_14));
  Multiplexer #(.enable("false")) multiplexer_7 (
    .in0(n4_bit_sub_3_out_10), .in1(A1), .out(multiplexer_7_out), .sel(n4_bit_sub_3_out_14));
  Multiplexer #(.enable("false")) multiplexer_8 (
    .in0(n4_bit_sub_3_out_11), .in1(multiplexer_4_out), .out(multiplexer_8_out), .sel(n4_bit_sub_3_out_14));
  Multiplexer #(.enable("false")) multiplexer_9 (
    .in0(n4_bit_sub_3_out_12), .in1(multiplexer_5_out), .out(multiplexer_9_out), .sel(n4_bit_sub_3_out_14));
  _4_Bit_Sub u_4_bit_sub_4 (
    .A0(A0), .B0(B0), .A1(multiplexer_7_out), .B1(B1), .A2(multiplexer_8_out), .B2(B2),
    .A3(multiplexer_9_out), .B3(B3), .CP(1'b0), .out_10(n4_bit_sub_1_out_13), .out_11(n4_bit_sub_1_out_13),
    .out_12(n4_bit_sub_1_out_13), .out_13(n4_bit_sub_1_out_13), .out_14(n4_bit_sub_4_out_14));
  not not_1 (Q0, n4_bit_sub_4_out_14);
  not not_2 (Q1, n4_bit_sub_3_out_14);
  not not_3 (Q2, n4_bit_sub_2_out_14);
  not not_4 (Q3, n4_bit_sub_1_out_14);
  xor xor_1 (SIGN, A_SIGN, B_SIGN);
  // also tied to GND on the sheet: n4_bit_sub_1_out_13

  // Notes on the sheet:
  //   0
  //   0
  //   0
  //   Q3
  //   Q2
  //   Q1
endmodule

module EX_Division (
  input  A3,
  input  A2,
  input  A1,
  input  A0,
  input  B3,
  input  B2,
  input  B1,
  input  B0,
  output Q0,
  output Q1,
  output Q2,
  output Q3
);

  Full_Division_With_Sign full_division_with_sign_1 (
    .A3(A3), .A2(A2), .A1(A1), .A0(A0), .B3(B3), .B2(B2), .B1(B1), .B0(B0), .Q0(Q0), .Q1(Q1), .Q2(Q2), .Q3(Q3));  // open: A_SIGN, B_SIGN, SIGN
endmodule

module Half_Adder (
  input  A0,
  input  B0,
  output S0,
  output C0
);

  xor xor_1 (S0, A0, B0);
  and and_1 (C0, A0, B0);
endmodule

module Full_Adder (
  input  A0,
  input  B0,
  input  C0,
  output SUM,
  output CARRY
);

  wire half_adder_1_c0, half_adder_1_s0, half_adder_2_c0;

  Half_Adder half_adder_1 (.A0(A0), .B0(B0), .S0(half_adder_1_s0), .C0(half_adder_1_c0));
  Half_Adder half_adder_2 (.A0(half_adder_1_s0), .B0(C0), .S0(SUM), .C0(half_adder_2_c0));
  or or_1 (CARRY, half_adder_2_c0, half_adder_1_c0);

  // Notes on the sheet:
  //   SUM
  //   Carry
endmodule

module _1_Bit_Comparator (
  input  A0,
  input  B0,
  output L0,
  output E0,
  output S0
);

  wire not_1_out, not_2_out, or_1_out;

  not not_1 (not_1_out, A0);
  not not_2 (not_2_out, B0);
  and and_1 (L0, A0, not_2_out);
  and and_2 (S0, B0, not_1_out);
  or or_1 (or_1_out, L0, S0);
  not not_3 (E0, or_1_out);
endmodule

module _4_Bit_Comparator (
  input  A0,
  input  B0,
  input  A1,
  input  B1,
  input  A2,
  input  B2,
  input  A3,
  input  B3,
  output L,
  output E,
  output S
);

  wire and_1_out, and_2_out, and_3_out, and_4_out, and_5_out, and_6_out, n1_bit_comparator_1_e0,
       n1_bit_comparator_1_l0, n1_bit_comparator_1_s0, n1_bit_comparator_2_e0, n1_bit_comparator_2_l0,
       n1_bit_comparator_2_s0, n1_bit_comparator_3_e0, n1_bit_comparator_3_l0, n1_bit_comparator_3_s0,
       n1_bit_comparator_4_e0, n1_bit_comparator_4_l0, n1_bit_comparator_4_s0;

  _1_Bit_Comparator u_1_bit_comparator_1 (
    .A0(A0), .B0(B0), .L0(n1_bit_comparator_1_l0), .E0(n1_bit_comparator_1_e0), .S0(n1_bit_comparator_1_s0));
  _1_Bit_Comparator u_1_bit_comparator_2 (
    .A0(A1), .B0(B1), .L0(n1_bit_comparator_2_l0), .E0(n1_bit_comparator_2_e0), .S0(n1_bit_comparator_2_s0));
  _1_Bit_Comparator u_1_bit_comparator_3 (
    .A0(A2), .B0(B2), .L0(n1_bit_comparator_3_l0), .E0(n1_bit_comparator_3_e0), .S0(n1_bit_comparator_3_s0));
  _1_Bit_Comparator u_1_bit_comparator_4 (
    .A0(A3), .B0(B3), .L0(n1_bit_comparator_4_l0), .E0(n1_bit_comparator_4_e0), .S0(n1_bit_comparator_4_s0));
  and and_1 (and_1_out, n1_bit_comparator_1_l0, n1_bit_comparator_2_e0, n1_bit_comparator_3_e0, n1_bit_comparator_4_e0);
  and and_2 (and_2_out, n1_bit_comparator_2_l0, n1_bit_comparator_3_e0, n1_bit_comparator_4_e0);
  and and_3 (and_3_out, n1_bit_comparator_3_l0, n1_bit_comparator_4_e0);
  and and_4 (and_4_out, n1_bit_comparator_1_s0, n1_bit_comparator_2_e0, n1_bit_comparator_3_e0, n1_bit_comparator_4_e0);
  and and_5 (and_5_out, n1_bit_comparator_2_s0, n1_bit_comparator_3_e0, n1_bit_comparator_4_e0);
  and and_6 (and_6_out, n1_bit_comparator_3_s0, n1_bit_comparator_4_e0);
  or or_1 (L, and_1_out, and_2_out, and_3_out, n1_bit_comparator_4_l0);
  or or_2 (S, and_4_out, and_5_out, and_6_out, n1_bit_comparator_4_s0);
  and and_7 (E, n1_bit_comparator_1_e0, n1_bit_comparator_2_e0, n1_bit_comparator_3_e0, n1_bit_comparator_4_e0);

  // Notes on the sheet:
  //   L1
  //   L2
  //   S2
  //   L3
  //   S3
  //   L0
  //   E0
  //   S0
  //   E1
  //   S1
  //   E2
  //   E3
endmodule

module Final_Multiplication_With_Sign (
  input  A0,
  input  B0,
  input  A1,
  input  B1,
  input  A2,
  input  B2,
  input  A3,
  input  B3,
  input  A4,
  input  B4,
  output C0,
  output C1,
  output C2,
  output C3,
  output C4,
  output C5,
  output C6,
  output C7,
  output C8_SIGN
);

  wire A0B1_out, A0B2_out, A0B3_out, A1B0_out, A1B1_out, A1B2_out, A1B3_out, A2B0_out, A2B1_out, A2B2_out,
       A2B3_out, A3B0_out, A3B1_out, A3B2_out, A3B3_out, final_addition_without_sign_1_c,
       final_addition_without_sign_1_s1, final_addition_without_sign_1_s2, final_addition_without_sign_1_s3,
       final_addition_without_sign_2_c, final_addition_without_sign_2_s1, final_addition_without_sign_2_s2,
       final_addition_without_sign_2_s3;

  xor For_SIGN (C8_SIGN, A4, B4);
  and A0B0 (C0, B0, A0);
  and A0B1 (A0B1_out, B1, A0);
  and A0B2 (A0B2_out, B2, A0);
  and A0B3 (A0B3_out, B3, A0);
  and A1B0 (A1B0_out, B0, A1);
  and A1B1 (A1B1_out, B1, A1);
  and A1B2 (A1B2_out, B2, A1);
  and A1B3 (A1B3_out, B3, A1);
  and A2B0 (A2B0_out, B0, A2);
  and A2B1 (A2B1_out, B1, A2);
  and A2B2 (A2B2_out, B2, A2);
  and A2B3 (A2B3_out, B3, A2);
  and A3B0 (A3B0_out, B0, A3);
  and A3B1 (A3B1_out, B1, A3);
  and A3B2 (A3B2_out, B2, A3);
  and A3B3 (A3B3_out, B3, A3);
  Final_Addition_WIthout_Sign final_addition_without_sign_1 (
    .A0(A0B1_out), .B0(A1B0_out), .A1(A0B2_out), .B1(A1B1_out), .A2(A0B3_out), .B2(A1B2_out), .A3(1'b0),
    .B3(A1B3_out), .in_9(1'b0), .S0(C1), .S1(final_addition_without_sign_1_s1),
    .S2(final_addition_without_sign_1_s2), .S3(final_addition_without_sign_1_s3),
    .C(final_addition_without_sign_1_c));
  Final_Addition_WIthout_Sign final_addition_without_sign_2 (
    .A0(final_addition_without_sign_1_s1), .B0(A2B0_out), .A1(final_addition_without_sign_1_s2),
    .B1(A2B1_out), .A2(final_addition_without_sign_1_s3), .B2(A2B2_out),
    .A3(final_addition_without_sign_1_c), .B3(A2B3_out), .in_9(1'b0), .S0(C2),
    .S1(final_addition_without_sign_2_s1), .S2(final_addition_without_sign_2_s2),
    .S3(final_addition_without_sign_2_s3), .C(final_addition_without_sign_2_c));
  Final_Addition_WIthout_Sign final_addition_without_sign_3 (
    .A0(final_addition_without_sign_2_s1), .B0(A3B0_out), .A1(final_addition_without_sign_2_s2),
    .B1(A3B1_out), .A2(final_addition_without_sign_2_s3), .B2(A3B2_out),
    .A3(final_addition_without_sign_2_c), .B3(A3B3_out), .in_9(1'b0), .S0(C3), .S1(C4), .S2(C5), .S3(C6),
    .C(C7));

  // Notes on the sheet:
  //   S0
  //   S1
  //   S2
  //   S3
  //   C
  //   C0
  //   C1
  //   K0
  //   K1
  //   K2
  //   K3
  //   C/
  //   C2
endmodule

module Final_Addition_WIthout_Sign (
  input  A0,
  input  B0,
  input  A1,
  input  B1,
  input  A2,
  input  B2,
  input  A3,
  input  B3,
  input  in_9,
  output S0,
  output S1,
  output S2,
  output S3,
  output C
);

  wire full_adder_1_carry, full_adder_2_carry, full_adder_3_carry, full_adder_4_carry;

  Full_Adder full_adder_1 (.A0(A0), .B0(B0), .C0(in_9), .SUM(S0), .CARRY(full_adder_1_carry));
  Full_Adder full_adder_2 (.A0(A1), .B0(B1), .C0(full_adder_1_carry), .SUM(S1), .CARRY(full_adder_2_carry));
  Full_Adder full_adder_3 (.A0(A2), .B0(B2), .C0(full_adder_2_carry), .SUM(S2), .CARRY(full_adder_3_carry));
  Full_Adder full_adder_4 (.A0(A3), .B0(B3), .C0(full_adder_3_carry), .SUM(S3), .CARRY(full_adder_4_carry));
  or or_1 (C, full_adder_4_carry, in_9);
endmodule

module _7_Bit_Sub (
  input  A0,
  input  B0,
  input  A1,
  input  B1,
  input  A2,
  input  B2,
  input  A3,
  input  B3,
  input  A4,
  input  B4,
  input  A5,
  input  B5,
  input  CP,
  input  in_14,
  input  in_15,
  output out_16,
  output out_17,
  output out_18,
  output out_19,
  output out_20,
  output out_21,
  output out_22
);

  wire full_subtractor_1_c, full_subtractor_2_c, full_subtractor_3_c, full_subtractor_4_c,
       full_subtractor_5_c, full_subtractor_6_c;

  Full_Subtractor full_subtractor_1 (.A(A0), .B(B0), .cp(CP), .S(out_16), .C(full_subtractor_1_c));
  Full_Subtractor full_subtractor_2 (.A(A1), .B(B1), .cp(full_subtractor_1_c), .S(out_17), .C(full_subtractor_2_c));
  Full_Subtractor full_subtractor_3 (.A(A2), .B(B2), .cp(full_subtractor_2_c), .S(out_18), .C(full_subtractor_3_c));
  Full_Subtractor full_subtractor_4 (.A(A3), .B(B3), .cp(full_subtractor_3_c), .S(out_19), .C(full_subtractor_4_c));
  Full_Subtractor full_subtractor_5 (.A(A4), .B(B4), .cp(full_subtractor_4_c), .S(out_20), .C(full_subtractor_5_c));
  Full_Subtractor full_subtractor_6 (.A(A5), .B(B5), .cp(full_subtractor_5_c), .S(out_21), .C(full_subtractor_6_c));
  Full_Subtractor full_subtractor_7 (.A(in_14), .B(in_15), .cp(full_subtractor_6_c), .S(out_22));  // open: C
endmodule

module _6_Bit_Adder (
  input  A0,
  input  B0,
  input  A1,
  input  B1,
  input  A2,
  input  B2,
  input  A3,
  input  B3,
  input  A4,
  input  B4,
  input  in_11,
  input  in_12,
  input  in_13,
  output S0,
  output S1,
  output S2,
  output S3,
  output out_18,
  output out_19,
  output out_20
);

  wire full_adder_1_carry, full_adder_2_carry, full_adder_3_carry, full_adder_4_carry, full_adder_5_carry;

  Full_Adder full_adder_1 (.A0(A0), .B0(B0), .C0(in_11), .SUM(S0), .CARRY(full_adder_1_carry));
  Full_Adder full_adder_2 (.A0(A1), .B0(B1), .C0(full_adder_1_carry), .SUM(S1), .CARRY(full_adder_2_carry));
  Full_Adder full_adder_3 (.A0(A2), .B0(B2), .C0(full_adder_2_carry), .SUM(S2), .CARRY(full_adder_3_carry));
  Full_Adder full_adder_4 (.A0(A3), .B0(B3), .C0(full_adder_3_carry), .SUM(S3), .CARRY(full_adder_4_carry));
  Full_Adder full_adder_5 (.A0(A4), .B0(B4), .C0(full_adder_4_carry), .SUM(out_18), .CARRY(full_adder_5_carry));
  Full_Adder full_adder_6 (.A0(in_12), .B0(in_13), .C0(full_adder_5_carry), .SUM(out_19), .CARRY(out_20));
endmodule

module _123 (
  input  A0,
  input  B0,
  input  A1,
  input  B1,
  input  A2,
  input  B2,
  input  A3,
  input  B3,
  input  A4,
  input  B4,
  input  A5_SIGN,
  input  B5_SIGN,
  output out_13,
  output out_14,
  output out_15,
  output out_16,
  output out_17,
  output out_18,
  output out_19
);

  wire and_1_out, and_2_out, and_3_out, full_adder_1_carry, full_adder_2_carry, full_adder_3_carry,
       full_adder_4_carry, full_adder_5_carry, n5_bit_comparator_1_p11, n5_bit_comparator_1_p12,
       n5_bit_comparator_1_p13, xor_1_out, xor_2_out, xor_3_out, xor_4_out, xor_5_out, xor_6_out;

  xor xor_1 (xor_1_out, B0, xor_6_out);
  xor xor_2 (xor_2_out, B1, xor_6_out);
  xor xor_3 (xor_3_out, B2, xor_6_out);
  xor xor_4 (xor_4_out, B3, xor_6_out);
  xor xor_5 (xor_5_out, B4, xor_6_out);
  Full_Adder full_adder_1 (.A0(A0), .B0(xor_1_out), .C0(xor_6_out), .SUM(out_13), .CARRY(full_adder_1_carry));
  xor xor_6 (xor_6_out, A5_SIGN, B5_SIGN);
  Full_Adder full_adder_2 (.A0(A1), .B0(xor_2_out), .C0(full_adder_1_carry), .SUM(out_14), .CARRY(full_adder_2_carry));
  Full_Adder full_adder_3 (.A0(A2), .B0(xor_3_out), .C0(full_adder_2_carry), .SUM(out_15), .CARRY(full_adder_3_carry));
  // _5_Bit_Comparator 5_bit_comparator_1: pin names not known; wires that end beside it: A0, B0, A1, B1, A2, B2, A3, B3, A4, xor_5_out, n5_bit_comparator_1_p11, n5_bit_comparator_1_p12, n5_bit_comparator_1_p13
  Full_Adder full_adder_4 (.A0(A3), .B0(xor_4_out), .C0(full_adder_3_carry), .SUM(out_16), .CARRY(full_adder_4_carry));
  Full_Adder full_adder_5 (.A0(A4), .B0(xor_5_out), .C0(full_adder_4_carry), .SUM(out_17), .CARRY(full_adder_5_carry));
  and and_1 (and_1_out, A5_SIGN, n5_bit_comparator_1_p11);
  and and_2 (and_2_out, n5_bit_comparator_1_p12, A5_SIGN, B5_SIGN);
  xor xor_7 (out_18, out_17, full_adder_5_carry);
  and and_3 (and_3_out, n5_bit_comparator_1_p13, B5_SIGN);
  or or_1 (out_19, and_1_out, and_2_out, and_3_out);
endmodule

module _5_Bit_Comparator (
  input  A0,
  input  B0,
  input  A1,
  input  B1,
  input  A2,
  input  B2,
  input  A3,
  input  B3,
  input  A4,
  input  B4,
  output L,
  output E,
  output S
);

  wire and_1_out, and_2_out, and_3_out, and_4_out, and_5_out, and_6_out, and_7_out, and_8_out,
       n1_bit_comparator_1_e0, n1_bit_comparator_1_l0, n1_bit_comparator_1_s0, n1_bit_comparator_2_e0,
       n1_bit_comparator_2_l0, n1_bit_comparator_2_s0, n1_bit_comparator_3_e0, n1_bit_comparator_3_l0,
       n1_bit_comparator_3_s0, n1_bit_comparator_4_e0, n1_bit_comparator_4_l0, n1_bit_comparator_4_s0,
       n1_bit_comparator_5_e0, n1_bit_comparator_5_l0, n1_bit_comparator_5_s0;

  _1_Bit_Comparator u_1_bit_comparator_1 (
    .A0(A3), .B0(B3), .L0(n1_bit_comparator_1_l0), .E0(n1_bit_comparator_1_e0), .S0(n1_bit_comparator_1_s0));
  _1_Bit_Comparator u_1_bit_comparator_2 (
    .A0(A4), .B0(B4), .L0(n1_bit_comparator_2_l0), .E0(n1_bit_comparator_2_e0), .S0(n1_bit_comparator_2_s0));
  _1_Bit_Comparator u_1_bit_comparator_3 (
    .A0(A0), .B0(B0), .L0(n1_bit_comparator_3_l0), .E0(n1_bit_comparator_3_e0), .S0(n1_bit_comparator_3_s0));
  _1_Bit_Comparator u_1_bit_comparator_4 (
    .A0(A1), .B0(B1), .L0(n1_bit_comparator_4_l0), .E0(n1_bit_comparator_4_e0), .S0(n1_bit_comparator_4_s0));
  _1_Bit_Comparator u_1_bit_comparator_5 (
    .A0(A2), .B0(B2), .L0(n1_bit_comparator_5_l0), .E0(n1_bit_comparator_5_e0), .S0(n1_bit_comparator_5_s0));
  and and_1 (and_1_out, n1_bit_comparator_2_e0, n1_bit_comparator_1_l0);
  and and_2 (and_2_out, n1_bit_comparator_1_s0, n1_bit_comparator_2_e0);
  and and_3 (and_3_out, n1_bit_comparator_3_l0, n1_bit_comparator_4_e0, n1_bit_comparator_2_e0, n1_bit_comparator_5_e0, n1_bit_comparator_1_e0);
  and and_4 (and_4_out, n1_bit_comparator_4_l0, n1_bit_comparator_2_e0, n1_bit_comparator_5_e0, n1_bit_comparator_1_e0);
  and and_5 (and_5_out, n1_bit_comparator_5_l0, n1_bit_comparator_2_e0, n1_bit_comparator_1_e0);
  and and_6 (and_6_out, n1_bit_comparator_3_s0, n1_bit_comparator_4_e0, n1_bit_comparator_5_e0, n1_bit_comparator_1_e0);
  and and_7 (and_7_out, n1_bit_comparator_4_s0, n1_bit_comparator_5_e0, n1_bit_comparator_1_e0);
  and and_8 (and_8_out, n1_bit_comparator_5_s0, n1_bit_comparator_1_e0);
  or or_1 (L, and_3_out, and_4_out, n1_bit_comparator_2_l0, and_5_out, and_1_out);
  or or_2 (S, and_6_out, and_7_out, n1_bit_comparator_2_s0, and_8_out, and_2_out);
  and and_9 (E, n1_bit_comparator_3_e0, n1_bit_comparator_4_e0, n1_bit_comparator_2_e0, n1_bit_comparator_5_e0, n1_bit_comparator_1_e0);

  // Notes on the sheet:
  //   L3
  //   L1
  //   L2
  //   S2
  //   S3
  //   L4
  //   E4
  //   S4
  //   L0
  //   E0
  //   S0
  //   E1
  //   S1
  //   E2
  //   E3
endmodule
