// Logisim project Final_Addition.circ as structural Verilog
module Half_Adder (
  input  A0,
  input  B0,
  output S0,
  output C0
);

  xor xor_1 (S0, A0, B0);
  and and_1 (C0, A0, B0);
endmodule

module Full_Adder (
  input  A0,
  input  B0,
  input  C0,
  output SUM,
  output CARRY
);

  wire half_adder_1_c0, half_adder_1_s0, half_adder_2_c0;

  Half_Adder half_adder_1 (.A0(A0), .B0(B0), .S0(half_adder_1_s0), .C0(half_adder_1_c0));
  Half_Adder half_adder_2 (.A0(half_adder_1_s0), .B0(C0), .S0(SUM), .C0(half_adder_2_c0));
  or or_1 (CARRY, half_adder_2_c0, half_adder_1_c0);

  // Notes on the sheet:
  //   SUM
  //   Carry
endmodule

module _1_Bit_Comparator (
  input  A0,
  input  B0,
  output L0,
  output E0,
  output S0
);

  wire not_1_out, not_2_out, or_1_out;

  not not_1 (not_1_out, A0);
  not not_2 (not_2_out, B0);
  and and_1 (L0, A0, not_2_out);
  and and_2 (S0, B0, not_1_out);
  or or_1 (or_1_out, L0, S0);
  not not_3 (E0, or_1_out);
endmodule

module _4_Bit_Comparator (
  input  A0,
  input  B0,
  input  A1,
  input  B1,
  input  A2,
  input  B2,
  input  A3,
  input  B3,
  output L,
  output E,
  output S
);

  wire and_1_out, and_2_out, and_3_out, and_4_out, and_5_out, and_6_out, n1_bit_comparator_1_e0,
       n1_bit_comparator_1_l0, n1_bit_comparator_1_s0, n1_bit_comparator_2_e0, n1_bit_comparator_2_l0,
       n1_bit_comparator_2_s0, n1_bit_comparator_3_e0, n1_bit_comparator_3_l0, n1_bit_comparator_3_s0,
       n1_bit_comparator_4_e0, n1_bit_comparator_4_l0, n1_bit_comparator_4_s0;

  _1_Bit_Comparator u_1_bit_comparator_1 (
    .A0(A0), .B0(B0), .L0(n1_bit_comparator_1_l0), .E0(n1_bit_comparator_1_e0), .S0(n1_bit_comparator_1_s0));
  _1_Bit_Comparator u_1_bit_comparator_2 (
    .A0(A1), .B0(B1), .L0(n1_bit_comparator_2_l0), .E0(n1_bit_comparator_2_e0), .S0(n1_bit_comparator_2_s0));
  _1_Bit_Comparator u_1_bit_comparator_3 (
    .A0(A2), .B0(B2), .L0(n1_bit_comparator_3_l0), .E0(n1_bit_comparator_3_e0), .S0(n1_bit_comparator_3_s0));
  _1_Bit_Comparator u_1_bit_comparator_4 (
    .A0(A3), .B0(B3), .L0(n1_bit_comparator_4_l0), .E0(n1_bit_comparator_4_e0), .S0(n1_bit_comparator_4_s0));
  and and_1 (and_1_out, n1_bit_comparator_1_l0, n1_bit_comparator_2_e0, n1_bit_comparator_3_e0, n1_bit_comparator_4_e0);
  and and_2 (and_2_out, n1_bit_comparator_2_l0, n1_bit_comparator_3_e0, n1_bit_comparator_4_e0);
  and and_3 (and_3_out, n1_bit_comparator_3_l0, n1_bit_comparator_4_e0);
  and and_4 (and_4_out, n1_bit_comparator_1_s0, n1_bit_comparator_2_e0, n1_bit_comparator_3_e0, n1_bit_comparator_4_e0);
  and and_5 (and_5_out, n1_bit_comparator_2_s0, n1_bit_comparator_3_e0, n1_bit_comparator_4_e0);
  and and_6 (and_6_out, n1_bit_comparator_3_s0, n1_bit_comparator_4_e0);
  or or_1 (L, and_1_out, and_2_out, and_3_out, n1_bit_comparator_4_l0);
  or or_2 (S, and_4_out, and_5_out, and_6_out, n1_bit_comparator_4_s0);
  and and_7 (E, n1_bit_comparator_1_e0, n1_bit_comparator_2_e0, n1_bit_comparator_3_e0, n1_bit_comparator_4_e0);

  // Notes on the sheet:
  //   L1
  //   L2
  //   S2
  //   L3
  //   S3
  //   L0
  //   E0
  //   S0
  //   E1
  //   S1
  //   E2
  //   E3
endmodule

module Final_Addition (
  input  A0,
  input  B0,
  input  A1,
  input  B1,
  input  A2,
  input  B2,
  input  A2_2,
  input  B3,
  input  in_9,
  input  A4_always_zero,
  input  B4_always_zero,
  input  A5_Sign,
  input  B5_Sign,
  output S0,
  output S1,
  output S2,
  output S3,
  output C,
  output Sign
);

  wire and_1_out, and_2_out, and_3_out, full_adder_1_carry, full_adder_2_carry, full_adder_3_carry,
       full_adder_4_carry, n4_bit_comparator_1_e, n4_bit_comparator_1_l, n4_bit_comparator_1_s;

  Full_Adder full_adder_1 (.A0(A0), .B0(B0), .C0(in_9), .SUM(S0), .CARRY(full_adder_1_carry));
  Full_Adder full_adder_2 (.A0(A1), .B0(B1), .C0(full_adder_1_carry), .SUM(S1), .CARRY(full_adder_2_carry));
  Full_Adder full_adder_3 (.A0(A2), .B0(B2), .C0(full_adder_2_carry), .SUM(S2), .CARRY(full_adder_3_carry));
  _4_Bit_Comparator u_4_bit_comparator_1 (
    .A0(A0), .B0(B0), .A1(A1), .B1(B1), .A2(A2), .B2(B2), .A3(A2_2), .B3(B3), .L(n4_bit_comparator_1_l),
    .E(n4_bit_comparator_1_e), .S(n4_bit_comparator_1_s));
  Full_Adder full_adder_4 (.A0(A2_2), .B0(B3), .C0(full_adder_3_carry), .SUM(S3), .CARRY(full_adder_4_carry));
  and and_1 (and_1_out, n4_bit_comparator_1_l, A5_Sign);
  and and_2 (and_2_out, n4_bit_comparator_1_e, B5_Sign, A5_Sign);
  and and_3 (and_3_out, n4_bit_comparator_1_s, B5_Sign);
  or or_1 (C, full_adder_4_carry, A4_always_zero, B4_always_zero);
  or or_2 (Sign, and_1_out, and_2_out, and_3_out);

  // Notes on the sheet:
  //   C(we can use A4 or B4 instead of the first carry as they all must be zeros)
  //   Sum
  //   Carry
  //   L
  //   E
  //   S
endmodule
