// Logisim project Final_Multiplixer.circ as structural Verilog
module Half_Adder (
  input  A0,
  input  B0,
  output S0,
  output C0
);

  xor xor_1 (S0, A0, B0);
  and and_1 (C0, A0, B0);
endmodule

module Full_Adder (
  input  A0,
  input  B0,
  input  C0,
  output SUM,
  output CARRY
);

  wire half_adder_1_c0, half_adder_1_s0, half_adder_2_c0;

  Half_Adder half_adder_1 (.A0(A0), .B0(B0), .S0(half_adder_1_s0), .C0(half_adder_1_c0));
  Half_Adder half_adder_2 (.A0(half_adder_1_s0), .B0(C0), .S0(SUM), .C0(half_adder_2_c0));
  or or_1 (CARRY, half_adder_2_c0, half_adder_1_c0);

  // Notes on the sheet:
  //   SUM
  //   Carry
endmodule

module _1_Bit_Comparator (
  input  A0,
  input  B0,
  output L0,
  output E0,
  output S0
);

  wire not_1_out, not_2_out, or_1_out;

  not not_1 (not_1_out, A0);
  not not_2 (not_2_out, B0);
  and and_1 (L0, A0, not_2_out);
  and and_2 (S0, B0, not_1_out);
  or or_1 (or_1_out, L0, S0);
  not not_3 (E0, or_1_out);
endmodule

module _4_Bit_Comparator (
  input  A0,
  input  B0,
  input  A1,
  input  B1,
  input  A2,
  input  B2,
  input  A3,
  input  B3,
  output L,
  output E,
  output S
);

  wire and_1_out, and_2_out, and_3_out, and_4_out, and_5_out, and_6_out, n1_bit_comparator_1_e0,
       n1_bit_comparator_1_l0, n1_bit_comparator_1_s0, n1_bit_comparator_2_e0, n1_bit_comparator_2_l0,
       n1_bit_comparator_2_s0, n1_bit_comparator_3_e0, n1_bit_comparator_3_l0, n1_bit_comparator_3_s0,
       n1_bit_comparator_4_e0, n1_bit_comparator_4_l0, n1_bit_comparator_4_s0;

  _1_Bit_Comparator u_1_bit_comparator_1 (
    .A0(A0), .B0(B0), .L0(n1_bit_comparator_1_l0), .E0(n1_bit_comparator_1_e0), .S0(n1_bit_comparator_1_s0));
  _1_Bit_Comparator u_1_bit_comparator_2 (
    .A0(A1), .B0(B1), .L0(n1_bit_comparator_2_l0), .E0(n1_bit_comparator_2_e0), .S0(n1_bit_comparator_2_s0));
  _1_Bit_Comparator u_1_bit_comparator_3 (
    .A0(A2), .B0(B2), .L0(n1_bit_comparator_3_l0), .E0(n1_bit_comparator_3_e0), .S0(n1_bit_comparator_3_s0));
  _1_Bit_Comparator u_1_bit_comparator_4 (
    .A0(A3), .B0(B3), .L0(n1_bit_comparator_4_l0), .E0(n1_bit_comparator_4_e0), .S0(n1_bit_comparator_4_s0));
  and and_1 (and_1_out, n1_bit_comparator_1_l0, n1_bit_comparator_2_e0, n1_bit_comparator_3_e0, n1_bit_comparator_4_e0);
  and and_2 (and_2_out, n1_bit_comparator_2_l0, n1_bit_comparator_3_e0, n1_bit_comparator_4_e0);
  and and_3 (and_3_out, n1_bit_comparator_3_l0, n1_bit_comparator_4_e0);
  and and_4 (and_4_out, n1_bit_comparator_1_s0, n1_bit_comparator_2_e0, n1_bit_comparator_3_e0, n1_bit_comparator_4_e0);
  and and_5 (and_5_out, n1_bit_comparator_2_s0, n1_bit_comparator_3_e0, n1_bit_comparator_4_e0);
  and and_6 (and_6_out, n1_bit_comparator_3_s0, n1_bit_comparator_4_e0);
  or or_1 (L, and_1_out, and_2_out, and_3_out, n1_bit_comparator_4_l0);
  or or_2 (S, and_4_out, and_5_out, and_6_out, n1_bit_comparator_4_s0);
  and and_7 (E, n1_bit_comparator_1_e0, n1_bit_comparator_2_e0, n1_bit_comparator_3_e0, n1_bit_comparator_4_e0);

  // Notes on the sheet:
  //   L1
  //   L2
  //   S2
  //   L3
  //   S3
  //   L0
  //   E0
  //   S0
  //   E1
  //   S1
  //   E2
  //   E3
endmodule

module Final_Addition_WIthout_Sign (
  input  A0,
  input  B0,
  input  A1,
  input  B1,
  input  A2,
  input  B2,
  input  A3,
  input  B3,
  input  in_9,
  output S0,
  output S1,
  output S2,
  output S3,
  output C
);

  wire full_adder_1_carry, full_adder_2_carry, full_adder_3_carry, full_adder_4_carry;

  Full_Adder full_adder_1 (.A0(A0), .B0(B0), .C0(in_9), .SUM(S0), .CARRY(full_adder_1_carry));
  Full_Adder full_adder_2 (.A0(A1), .B0(B1), .C0(full_adder_1_carry), .SUM(S1), .CARRY(full_adder_2_carry));
  Full_Adder full_adder_3 (.A0(A2), .B0(B2), .C0(full_adder_2_carry), .SUM(S2), .CARRY(full_adder_3_carry));
  Full_Adder full_adder_4 (.A0(A3), .B0(B3), .C0(full_adder_3_carry), .SUM(S3), .CARRY(full_adder_4_carry));
  or or_1 (C, full_adder_4_carry, in_9);

  // Notes on the sheet:
  //   Carry in(always 0)
endmodule

module Multiplixer (
  input  A0,
  input  B0,
  input  A1,
  input  B1,
  input  A2,
  input  B2,
  input  A3,
  input  B3,
  input  A4,
  input  B4,
  output C0,
  output C1,
  output C2,
  output C3,
  output C4,
  output C5,
  output C6,
  output C7,
  output C8_SIGN
);

  wire A0B1_out, A0B2_out, A0B3_out, A1B0_out, A1B1_out, A1B2_out, A1B3_out, A2B0_out, A2B1_out, A2B2_out,
       A2B3_out, A3B0_out, A3B1_out, A3B2_out, A3B3_out, final_addition_without_sign_1_c,
       final_addition_without_sign_1_s1, final_addition_without_sign_1_s2, final_addition_without_sign_1_s3,
       final_addition_without_sign_2_c, final_addition_without_sign_2_s1, final_addition_without_sign_2_s2,
       final_addition_without_sign_2_s3;

  xor For_SIGN (C8_SIGN, A4, B4);
  and A0B0 (C0, B0, A0);
  and A0B1 (A0B1_out, B1, A0);
  and A0B2 (A0B2_out, B2, A0);
  and A0B3 (A0B3_out, B3, A0);
  and A1B0 (A1B0_out, B0, A1);
  and A1B1 (A1B1_out, B1, A1);
  and A1B2 (A1B2_out, B2, A1);
  and A1B3 (A1B3_out, B3, A1);
  and A2B0 (A2B0_out, B0, A2);
  and A2B1 (A2B1_out, B1, A2);
  and A2B2 (A2B2_out, B2, A2);
  and A2B3 (A2B3_out, B3, A2);
  and A3B0 (A3B0_out, B0, A3);
  and A3B1 (A3B1_out, B1, A3);
  and A3B2 (A3B2_out, B2, A3);
  and A3B3 (A3B3_out, B3, A3);
  Final_Addition_WIthout_Sign final_addition_without_sign_1 (
    .A0(A0B1_out), .B0(A1B0_out), .A1(A0B2_out), .B1(A1B1_out), .A2(A0B3_out), .B2(A1B2_out), .A3(1'b0),
    .B3(A1B3_out), .in_9(1'b0), .S0(C1), .S1(final_addition_without_sign_1_s1),
    .S2(final_addition_without_sign_1_s2), .S3(final_addition_without_sign_1_s3),
    .C(final_addition_without_sign_1_c));
  Final_Addition_WIthout_Sign final_addition_without_sign_2 (
    .A0(final_addition_without_sign_1_s1), .B0(A2B0_out), .A1(final_addition_without_sign_1_s2),
    .B1(A2B1_out), .A2(final_addition_without_sign_1_s3), .B2(A2B2_out),
    .A3(final_addition_without_sign_1_c), .B3(A2B3_out), .in_9(1'b0), .S0(C2),
    .S1(final_addition_without_sign_2_s1), .S2(final_addition_without_sign_2_s2),
    .S3(final_addition_without_sign_2_s3), .C(final_addition_without_sign_2_c));
  Final_Addition_WIthout_Sign final_addition_without_sign_3 (
    .A0(final_addition_without_sign_2_s1), .B0(A3B0_out), .A1(final_addition_without_sign_2_s2),
    .B1(A3B1_out), .A2(final_addition_without_sign_2_s3), .B2(A3B2_out),
    .A3(final_addition_without_sign_2_c), .B3(A3B3_out), .in_9(1'b0), .S0(C3), .S1(C4), .S2(C5), .S3(C6),
    .C(C7));

  // Notes on the sheet:
  //   Carry in
  //   S0
  //   S1
  //   S2
  //   S3
  //   C
  //   C0
  //   C1
  //   K0
  //   K1
  //   K2
  //   K3
  //   C/
  //   C2
endmodule

module Full_Subtractor (
  input  A,
  input  B,
  input  cp,
  output S,
  output C
);

  wire and_1_out, and_2_out, and_3_out, not_1_out;

  not not_1 (not_1_out, A);
  xor xor_1 (S, A, B, cp);
  and and_1 (and_1_out, not_1_out, B);
  and and_2 (and_2_out, not_1_out, cp);
  and and_3 (and_3_out, B, cp);
  or or_1 (C, and_1_out, and_2_out, and_3_out);
endmodule

module _4_Bit_Sub (
  input  A0,
  input  B0,
  input  A1,
  input  B1,
  input  A2,
  input  B2,
  input  A3,
  input  B3,
  input  CP,
  output out_10,
  output out_11,
  output out_12,
  output out_13
);

  wire full_subtractor_1_c, full_subtractor_2_c, full_subtractor_3_c, full_subtractor_4_c;

  Full_Subtractor full_subtractor_1 (.A(A0), .B(B0), .cp(CP), .S(out_10), .C(full_subtractor_1_c));
  Full_Subtractor full_subtractor_2 (.A(A1), .B(B1), .cp(full_subtractor_1_c), .S(out_11), .C(full_subtractor_2_c));
  Full_Subtractor full_subtractor_3 (.A(A2), .B(B2), .cp(full_subtractor_2_c), .S(out_12), .C(full_subtractor_3_c));
  Full_Subtractor full_subtractor_4 (.A(A3), .B(B3), .cp(full_subtractor_3_c), .S(out_13), .C(full_subtractor_4_c));
  // also tied to GND on the sheet: full_subtractor_4_c
endmodule
