// Logisim project Final_Project.circ as structural Verilog: 18 circuits, main circuit 1-Bit Comparator
module _1_Bit_Comparator (
  input  A0,
  input  B0,
  output L0,
  output E0,
  output S0
);

  wire not_1_out, not_2_out, or_1_out;

  not not_1 (not_1_out, A0);
  not not_2 (not_2_out, B0);
  and and_1 (L0, A0, not_2_out);
  and and_2 (S0, B0, not_1_out);
  or or_1 (or_1_out, L0, S0);
  not not_3 (E0, or_1_out);
endmodule

module _4_Bit_Comparator (
  input  A0,
  input  B0,
  input  A1,
  input  B1,
  input  A2,
  input  B2,
  input  A3,
  input  B3,
  output L,
  output E,
  output S
);

  wire and_1_out, and_2_out, and_3_out, and_4_out, and_5_out, and_6_out, and_7_out, and_8_out, and_9_out,
       and_10_out, and_11_out, and_12_out, and_13_out, and_14_out, n1_bit_comparator_1_e0,
       n1_bit_comparator_1_l0, n1_bit_comparator_1_s0, n1_bit_comparator_2_e0, n1_bit_comparator_2_l0,
       n1_bit_comparator_2_s0, n1_bit_comparator_3_e0, n1_bit_comparator_3_l0, n1_bit_comparator_3_s0,
       n1_bit_comparator_4_e0, n1_bit_comparator_4_l0, n1_bit_comparator_4_s0, or_1_out, or_2_out, or_3_out,
       or_4_out;

  _1_Bit_Comparator u_1_bit_comparator_1 (
    .A0(A0), .B0(B0), .L0(n1_bit_comparator_1_l0), .E0(n1_bit_comparator_1_e0), .S0(n1_bit_comparator_1_s0));
  _1_Bit_Comparator u_1_bit_comparator_2 (
    .A0(A1), .B0(B1), .L0(n1_bit_comparator_2_l0), .E0(n1_bit_comparator_2_e0), .S0(n1_bit_comparator_2_s0));
  _1_Bit_Comparator u_1_bit_comparator_3 (
    .A0(A2), .B0(B2), .L0(n1_bit_comparator_3_l0), .E0(n1_bit_comparator_3_e0), .S0(n1_bit_comparator_3_s0));
  _1_Bit_Comparator u_1_bit_comparator_4 (
    .A0(A3), .B0(B3), .L0(n1_bit_comparator_4_l0), .E0(n1_bit_comparator_4_e0), .S0(n1_bit_comparator_4_s0));
  and and_1 (and_1_out, n1_bit_comparator_2_l0, n1_bit_comparator_3_e0);
  and and_2 (and_2_out, n1_bit_comparator_2_s0, n1_bit_comparator_3_e0);
  and and_3 (and_3_out, n1_bit_comparator_1_l0, n1_bit_comparator_2_e0);
  and and_4 (and_4_out, and_3_out, and_5_out);
  and and_5 (and_5_out, n1_bit_comparator_3_e0, n1_bit_comparator_4_e0);
  and and_6 (and_6_out, and_1_out, n1_bit_comparator_4_e0);
  and and_7 (and_7_out, n1_bit_comparator_3_l0, n1_bit_comparator_4_e0);
  and and_8 (and_8_out, n1_bit_comparator_1_s0, n1_bit_comparator_2_e0);
  and and_9 (and_9_out, n1_bit_comparator_3_e0, n1_bit_comparator_4_e0);
  and and_10 (and_10_out, and_2_out, n1_bit_comparator_4_e0);
  and and_11 (and_11_out, n1_bit_comparator_3_s0, n1_bit_comparator_4_e0);
  and and_12 (and_12_out, and_8_out, and_9_out);
  or or_1 (or_1_out, and_4_out, and_6_out);
  or or_2 (or_2_out, and_7_out, n1_bit_comparator_4_l0);
  and and_13 (and_13_out, n1_bit_comparator_1_e0, n1_bit_comparator_2_e0);
  and and_14 (and_14_out, n1_bit_comparator_3_e0, n1_bit_comparator_4_e0);
  or or_3 (or_3_out, and_12_out, and_10_out);
  or or_4 (or_4_out, and_11_out, n1_bit_comparator_4_s0);
  or or_5 (L, or_1_out, or_2_out);
  and and_15 (E, and_13_out, and_14_out);
  or or_6 (S, or_3_out, or_4_out);

  // Notes on the sheet:
  //   L1
  //   L2
  //   S2
  //   L3
  //   S3
  //   L0
  //   E0
  //   S0
  //   E1
  //   S1
  //   E2
  //   E3
endmodule

module _5_Bit_Comparator (
  input  A0,
  input  B0,
  input  A1,
  input  B1,
  input  A2,
  input  B2,
  input  A3,
  input  B3,
  input  A4,
  input  B4,
  output L,
  output E,
  output S
);

  wire and_1_out, and_2_out, and_3_out, and_4_out, and_5_out, and_6_out, and_7_out, and_8_out, and_9_out,
       and_10_out, and_11_out, and_12_out, and_13_out, and_14_out, and_15_out, and_16_out, and_17_out,
       and_18_out, and_19_out, and_20_out, n1_bit_comparator_1_e0, n1_bit_comparator_1_l0,
       n1_bit_comparator_1_s0, n1_bit_comparator_2_e0, n1_bit_comparator_2_l0, n1_bit_comparator_2_s0,
       n1_bit_comparator_3_e0, n1_bit_comparator_3_l0, n1_bit_comparator_3_s0, n1_bit_comparator_4_e0,
       n1_bit_comparator_4_l0, n1_bit_comparator_4_s0, n1_bit_comparator_5_e0, n1_bit_comparator_5_l0,
       n1_bit_comparator_5_s0, or_1_out, or_2_out, or_3_out, or_4_out, or_5_out, or_7_out;

  _1_Bit_Comparator u_1_bit_comparator_1 (
    .A0(A3), .B0(B3), .L0(n1_bit_comparator_1_l0), .E0(n1_bit_comparator_1_e0), .S0(n1_bit_comparator_1_s0));
  _1_Bit_Comparator u_1_bit_comparator_2 (
    .A0(A4), .B0(B4), .L0(n1_bit_comparator_2_l0), .E0(n1_bit_comparator_2_e0), .S0(n1_bit_comparator_2_s0));
  _1_Bit_Comparator u_1_bit_comparator_3 (
    .A0(A0), .B0(B0), .L0(n1_bit_comparator_3_l0), .E0(n1_bit_comparator_3_e0), .S0(n1_bit_comparator_3_s0));
  _1_Bit_Comparator u_1_bit_comparator_4 (
    .A0(A1), .B0(B1), .L0(n1_bit_comparator_4_l0), .E0(n1_bit_comparator_4_e0), .S0(n1_bit_comparator_4_s0));
  _1_Bit_Comparator u_1_bit_comparator_5 (
    .A0(A2), .B0(B2), .L0(n1_bit_comparator_5_l0), .E0(n1_bit_comparator_5_e0), .S0(n1_bit_comparator_5_s0));
  and and_1 (and_1_out, n1_bit_comparator_2_e0, n1_bit_comparator_1_l0);
  and and_2 (and_2_out, n1_bit_comparator_1_s0, n1_bit_comparator_2_e0);
  and and_3 (and_3_out, n1_bit_comparator_3_l0, n1_bit_comparator_4_e0);
  and and_4 (and_4_out, n1_bit_comparator_2_e0, n1_bit_comparator_5_e0);
  and and_5 (and_5_out, n1_bit_comparator_4_l0, n1_bit_comparator_2_e0);
  and and_6 (and_6_out, n1_bit_comparator_5_e0, n1_bit_comparator_1_e0);
  and and_7 (and_7_out, n1_bit_comparator_5_l0, n1_bit_comparator_2_e0);
  and and_8 (and_8_out, n1_bit_comparator_4_s0, n1_bit_comparator_5_e0);
  and and_9 (and_9_out, and_3_out, and_4_out);
  and and_10 (and_10_out, and_5_out, and_6_out);
  and and_11 (and_11_out, and_7_out, n1_bit_comparator_1_e0);
  and and_12 (and_12_out, n1_bit_comparator_3_s0, n1_bit_comparator_4_e0);
  and and_13 (and_13_out, and_12_out, and_14_out);
  and and_14 (and_14_out, n1_bit_comparator_5_e0, n1_bit_comparator_1_e0);
  and and_15 (and_15_out, and_8_out, n1_bit_comparator_1_e0);
  and and_16 (and_16_out, n1_bit_comparator_5_s0, n1_bit_comparator_1_e0);
  and and_17 (and_17_out, and_9_out, n1_bit_comparator_1_e0);
  or or_1 (or_1_out, and_17_out, and_10_out);
  or or_2 (or_2_out, n1_bit_comparator_2_l0, and_11_out);
  or or_3 (or_3_out, and_13_out, and_15_out);
  or or_4 (or_4_out, n1_bit_comparator_2_s0, and_16_out);
  or or_5 (or_5_out, or_1_out, or_2_out);
  or or_6 (L, or_5_out, and_1_out);
  and and_18 (and_18_out, n1_bit_comparator_3_e0, n1_bit_comparator_4_e0);
  and and_19 (and_19_out, and_18_out, and_20_out);
  and and_20 (and_20_out, n1_bit_comparator_2_e0, n1_bit_comparator_5_e0);
  or or_7 (or_7_out, or_3_out, or_4_out);
  or or_8 (S, or_7_out, and_2_out);
  and and_21 (E, and_19_out, n1_bit_comparator_1_e0);

  // Notes on the sheet:
  //   L3
  //   L1
  //   L2
  //   S2
  //   S3
  //   L4
  //   E4
  //   S4
  //   L0
  //   E0
  //   S0
  //   E1
  //   S1
  //   E2
  //   E3
endmodule

module Half_Adder (
  input  A0,
  input  B0,
  output S0,
  output C0
);

  xor xor_1 (S0, A0, B0);
  and and_1 (C0, A0, B0);
endmodule

module Full_Adder (
  input  A0,
  input  B0,
  input  C0,
  output SUM,
  output CARRY
);

  wire half_adder_1_c0, half_adder_1_s0, half_adder_2_c0;

  Half_Adder half_adder_1 (.A0(A0), .B0(B0), .S0(half_adder_1_s0), .C0(half_adder_1_c0));
  Half_Adder half_adder_2 (.A0(half_adder_1_s0), .B0(C0), .S0(SUM), .C0(half_adder_2_c0));
  or or_1 (CARRY, half_adder_2_c0, half_adder_1_c0);

  // Notes on the sheet:
  //   SUM
  //   Carry
endmodule

module _4_Bit_Adder (
  input  A0,
  input  B0,
  input  A1,
  input  B1,
  input  A2,
  input  B2,
  input  A3,
  input  B3,
  input  in_9,
  output S0,
  output S1,
  output S2,
  output S3,
  output C
);

  wire full_adder_1_carry, full_adder_2_carry, full_adder_3_carry, full_adder_4_carry;

  Full_Adder full_adder_1 (.A0(A0), .B0(B0), .C0(in_9), .SUM(S0), .CARRY(full_adder_1_carry));
  Full_Adder full_adder_2 (.A0(A1), .B0(B1), .C0(full_adder_1_carry), .SUM(S1), .CARRY(full_adder_2_carry));
  Full_Adder full_adder_3 (.A0(A2), .B0(B2), .C0(full_adder_2_carry), .SUM(S2), .CARRY(full_adder_3_carry));
  Full_Adder full_adder_4 (.A0(A3), .B0(B3), .C0(full_adder_3_carry), .SUM(S3), .CARRY(full_adder_4_carry));
  or or_1 (C, full_adder_4_carry, in_9);
endmodule

module Final_Adder (
  input  [5:0] A,
  input  [5:0] B,
  output [7:0] Result,
  output Sign_Output
);

  wire and_1_out, and_2_out, and_3_out, and_4_out, full_adder_1_carry, full_adder_2_carry,
       full_adder_3_carry, full_adder_4_carry, n5_bit_comparator_1_e, n5_bit_comparator_1_l,
       n5_bit_comparator_1_s, xor_1_out, xor_2_out, xor_3_out, xor_4_out, xor_5_out, xor_6_out;

  xor xor_1 (xor_1_out, B[0], xor_6_out);
  xor xor_2 (xor_2_out, B[1], xor_6_out);
  xor xor_3 (xor_3_out, B[2], xor_6_out);
  xor xor_4 (xor_4_out, B[3], xor_6_out);
  xor xor_5 (xor_5_out, B[4], xor_6_out);
  Full_Adder full_adder_1 (.A0(A[0]), .B0(xor_1_out), .C0(xor_6_out), .SUM(Result[0]), .CARRY(full_adder_1_carry));
  xor xor_6 (xor_6_out, A[5], B[5]);
  Full_Adder full_adder_2 (
    .A0(A[1]), .B0(xor_2_out), .C0(full_adder_1_carry), .SUM(Result[1]), .CARRY(full_adder_2_carry));
  Full_Adder full_adder_3 (
    .A0(A[2]), .B0(xor_3_out), .C0(full_adder_2_carry), .SUM(Result[2]), .CARRY(full_adder_3_carry));
  _5_Bit_Comparator u_5_bit_comparator_1 (
    .A0(A[0]), .B0(B[0]), .A1(A[1]), .B1(B[1]), .A2(A[2]), .B2(B[2]), .A3(A[3]), .B3(B[3]), .A4(A[4]),
    .B4(B[4]), .L(n5_bit_comparator_1_l), .E(n5_bit_comparator_1_e), .S(n5_bit_comparator_1_s));
  Full_Adder full_adder_4 (
    .A0(A[3]), .B0(xor_4_out), .C0(full_adder_3_carry), .SUM(Result[3]), .CARRY(full_adder_4_carry));
  Full_Adder full_adder_5 (.A0(A[4]), .B0(xor_5_out), .C0(full_adder_4_carry), .SUM(Result[4]));  // open: CARRY
  and and_1 (and_1_out, A[5], n5_bit_comparator_1_l);
  and and_2 (and_2_out, A[5], n5_bit_comparator_1_e);
  and and_3 (and_3_out, and_2_out, B[5]);
  and and_4 (and_4_out, n5_bit_comparator_1_s, B[5]);
  or or_1 (Sign_Output, and_1_out, and_3_out, and_4_out);

  assign Result[7:5] = 3'b000;

  // Notes on the sheet:
  //   For Only Bits Number 5,6,7 As they always will be 0 As the OutPut Must be 5 Bits Without Sign
endmodule

module Final_Adder_2 (
  input  [4:0] A,
  input  [4:0] B,
  output [7:0] Result,
  output Sign_Output
);

  wire and_1_out, and_2_out, and_3_out, and_4_out, full_adder_1_carry, full_adder_2_carry,
       full_adder_3_carry, full_adder_4_carry, n5_bit_comparator_1_e, n5_bit_comparator_1_l,
       n5_bit_comparator_1_s, xor_1_out, xor_2_out, xor_3_out, xor_4_out, xor_5_out, xor_6_out;

  xor xor_1 (xor_1_out, B[0], xor_6_out);
  xor xor_2 (xor_2_out, B[1], xor_6_out);
  xor xor_3 (xor_3_out, B[2], xor_6_out);
  xor xor_4 (xor_4_out, B[3], xor_6_out);
  xor xor_5 (xor_5_out, 1'b0, xor_6_out);
  Full_Adder full_adder_1 (.A0(A[0]), .B0(xor_1_out), .C0(xor_6_out), .SUM(Result[0]), .CARRY(full_adder_1_carry));
  xor xor_6 (xor_6_out, A[4], B[4]);
  Full_Adder full_adder_2 (
    .A0(A[1]), .B0(xor_2_out), .C0(full_adder_1_carry), .SUM(Result[1]), .CARRY(full_adder_2_carry));
  Full_Adder full_adder_3 (
    .A0(A[2]), .B0(xor_3_out), .C0(full_adder_2_carry), .SUM(Result[2]), .CARRY(full_adder_3_carry));
  _5_Bit_Comparator u_5_bit_comparator_1 (
    .A0(A[0]), .B0(B[0]), .A1(A[1]), .B1(B[1]), .A2(A[2]), .B2(B[2]), .A3(A[3]), .B3(B[3]), .A4(1'b0),
    .B4(1'b0), .L(n5_bit_comparator_1_l), .E(n5_bit_comparator_1_e), .S(n5_bit_comparator_1_s));
  Full_Adder full_adder_4 (
    .A0(A[3]), .B0(xor_4_out), .C0(full_adder_3_carry), .SUM(Result[3]), .CARRY(full_adder_4_carry));
  Full_Adder full_adder_5 (.A0(1'b0), .B0(xor_5_out), .C0(full_adder_4_carry), .SUM(Result[4]));  // open: CARRY
  and and_1 (and_1_out, A[4], n5_bit_comparator_1_l);
  and and_2 (and_2_out, A[4], n5_bit_comparator_1_e);
  and and_3 (and_3_out, and_2_out, B[4]);
  and and_4 (and_4_out, n5_bit_comparator_1_s, B[4]);
  or or_1 (Sign_Output, and_1_out, and_3_out, and_4_out);

  assign Result[7:5] = 3'b000;

  // Notes on the sheet:
  //   For Only Bits Number 5,6,7 As they always will be 0 As the OutPut Must be 5 Bits Without Sign
endmodule

module Full_Subtractor (
  input  A,
  input  B,
  input  cp,
  output S,
  output C
);

  wire and_1_out, and_2_out, and_3_out, not_1_out, or_1_out, xor_1_out;

  not not_1 (not_1_out, A);
  xor xor_1 (xor_1_out, A, B);
  and and_1 (and_1_out, not_1_out, B);
  and and_2 (and_2_out, not_1_out, cp);
  and and_3 (and_3_out, B, cp);
  xor xor_2 (S, xor_1_out, cp);
  or or_1 (or_1_out, and_1_out, and_2_out);
  or or_2 (C, or_1_out, and_3_out);
endmodule

module _4_Bit_Subtractor (
  input  A0,
  input  B0,
  input  A1,
  input  B1,
  input  A2,
  input  B2,
  input  A3,
  input  B3,
  input  CP,
  output out_10,
  output out_11,
  output out_12,
  output out_13,
  output out_14
);

  wire full_subtractor_1_c, full_subtractor_2_c, full_subtractor_3_c;

  Full_Subtractor full_subtractor_1 (.A(A0), .B(B0), .cp(CP), .S(out_10), .C(full_subtractor_1_c));
  Full_Subtractor full_subtractor_2 (.A(A1), .B(B1), .cp(full_subtractor_1_c), .S(out_11), .C(full_subtractor_2_c));
  Full_Subtractor full_subtractor_3 (.A(A2), .B(B2), .cp(full_subtractor_2_c), .S(out_12), .C(full_subtractor_3_c));
  Full_Subtractor full_subtractor_4 (.A(A3), .B(B3), .cp(full_subtractor_3_c), .S(out_13), .C(out_14));
endmodule

module Final_Subtraction (
  input  [4:0] A,
  input  [4:0] B,
  output [7:0] Result,
  output Sign_Output
);

  wire and_1_out, and_2_out, and_3_out, and_4_out, full_adder_1_carry, full_adder_2_carry,
       full_adder_3_carry, full_adder_4_carry, n4_bit_comparator_1_e, n4_bit_comparator_1_l,
       n4_bit_comparator_1_s, xnor_1_out, xor_1_out, xor_2_out, xor_3_out, xor_4_out;

  xor xor_1 (xor_1_out, B[0], xnor_1_out);
  xor xor_2 (xor_2_out, B[1], xnor_1_out);
  xor xor_3 (xor_3_out, B[2], xnor_1_out);
  xor xor_4 (xor_4_out, B[3], xnor_1_out);
  xnor xnor_1 (xnor_1_out, A[4], B[4]);
  Full_Adder full_adder_1 (.A0(A[0]), .B0(xor_1_out), .C0(xnor_1_out), .SUM(Result[0]), .CARRY(full_adder_1_carry));
  Full_Adder full_adder_2 (
    .A0(A[1]), .B0(xor_2_out), .C0(full_adder_1_carry), .SUM(Result[1]), .CARRY(full_adder_2_carry));
  Full_Adder full_adder_3 (
    .A0(A[2]), .B0(xor_3_out), .C0(full_adder_2_carry), .SUM(Result[2]), .CARRY(full_adder_3_carry));
  _4_Bit_Comparator u_4_bit_comparator_1 (
    .A0(A[0]), .B0(B[0]), .A1(A[1]), .B1(B[1]), .A2(A[2]), .B2(B[2]), .A3(A[3]), .B3(B[3]),
    .L(n4_bit_comparator_1_l), .E(n4_bit_comparator_1_e), .S(n4_bit_comparator_1_s));
  Full_Adder full_adder_4 (
    .A0(A[3]), .B0(xor_4_out), .C0(full_adder_3_carry), .SUM(Result[3]), .CARRY(full_adder_4_carry));
  and and_1 (and_1_out, A[4], n4_bit_comparator_1_l);
  and and_2 (and_2_out, A[4], n4_bit_comparator_1_e);
  and and_3 (and_3_out, n4_bit_comparator_1_s, B[4]);
  or or_1 (Sign_Output, and_1_out, and_4_out, and_3_out);
  and and_4 (and_4_out, and_2_out, B[4]);

  assign Result[7:4] = 4'b0000;

  // Notes on the sheet:
  //   For Only Bits Number 4,5,6,7 As they always will be 0 As the OutPut Must be 4 Bits Without Sign
endmodule

module Final_Multiplication (
  input  [4:0] A,
  input  [4:0] B,
  output [7:0] Result,
  output C8_SIGN
);

  wire A0B1_out, A0B2_out, A0B3_out, A1B0_out, A1B1_out, A1B2_out, A1B3_out, A2B0_out, A2B1_out, A2B2_out,
       A2B3_out, A3B0_out, A3B1_out, A3B2_out, A3B3_out, n4_bit_adder_1_c, n4_bit_adder_1_s1,
       n4_bit_adder_1_s2, n4_bit_adder_1_s3, n4_bit_adder_2_c, n4_bit_adder_2_s1, n4_bit_adder_2_s2,
       n4_bit_adder_2_s3;

  xor For_SIGN (C8_SIGN, A[4], B[4]);
  and A0B0 (Result[0], B[0], A[0]);
  and A0B1 (A0B1_out, B[1], A[0]);
  and A0B2 (A0B2_out, B[2], A[0]);
  and A0B3 (A0B3_out, B[3], A[0]);
  and A1B0 (A1B0_out, B[0], A[1]);
  and A1B1 (A1B1_out, B[1], A[1]);
  and A1B2 (A1B2_out, B[2], A[1]);
  and A1B3 (A1B3_out, B[3], A[1]);
  and A2B0 (A2B0_out, B[0], A[2]);
  and A2B1 (A2B1_out, B[1], A[2]);
  and A2B2 (A2B2_out, B[2], A[2]);
  and A2B3 (A2B3_out, B[3], A[2]);
  and A3B0 (A3B0_out, B[0], A[3]);
  and A3B1 (A3B1_out, B[1], A[3]);
  and A3B2 (A3B2_out, B[2], A[3]);
  and A3B3 (A3B3_out, B[3], A[3]);
  _4_Bit_Adder u_4_bit_adder_1 (
    .A0(A0B1_out), .B0(A1B0_out), .A1(A0B2_out), .B1(A1B1_out), .A2(A0B3_out), .B2(A1B2_out), .A3(1'b0),
    .B3(A1B3_out), .in_9(1'b0), .S0(Result[1]), .S1(n4_bit_adder_1_s1), .S2(n4_bit_adder_1_s2),
    .S3(n4_bit_adder_1_s3), .C(n4_bit_adder_1_c));
  _4_Bit_Adder u_4_bit_adder_2 (
    .A0(n4_bit_adder_1_s1), .B0(A2B0_out), .A1(n4_bit_adder_1_s2), .B1(A2B1_out), .A2(n4_bit_adder_1_s3),
    .B2(A2B2_out), .A3(n4_bit_adder_1_c), .B3(A2B3_out), .in_9(1'b0), .S0(Result[2]), .S1(n4_bit_adder_2_s1),
    .S2(n4_bit_adder_2_s2), .S3(n4_bit_adder_2_s3), .C(n4_bit_adder_2_c));
  _4_Bit_Adder u_4_bit_adder_3 (
    .A0(n4_bit_adder_2_s1), .B0(A3B0_out), .A1(n4_bit_adder_2_s2), .B1(A3B1_out), .A2(n4_bit_adder_2_s3),
    .B2(A3B2_out), .A3(n4_bit_adder_2_c), .B3(A3B3_out), .in_9(1'b0), .S0(Result[3]), .S1(Result[4]),
    .S2(Result[5]), .S3(Result[6]), .C(Result[7]));

  // Notes on the sheet:
  //   S0
  //   S1
  //   S2
  //   S3
  //   C
  //   C0
  //   C1
  //   K0
  //   K1
  //   K2
  //   K3
  //   C/
  //   C2
endmodule

module Final_Division (
  input  [4:0] A,
  input  [4:0] B,
  output [7:0] Result,
  output SIGN
);

  wire multiplexer_1_out, multiplexer_2_out, multiplexer_3_out, multiplexer_4_out, multiplexer_5_out,
       multiplexer_6_out, multiplexer_7_out, multiplexer_8_out, multiplexer_9_out,
       n4_bit_subtractor_1_out_10, n4_bit_subtractor_1_out_11, n4_bit_subtractor_1_out_12,
       n4_bit_subtractor_1_out_13, n4_bit_subtractor_1_out_14, n4_bit_subtractor_2_out_10,
       n4_bit_subtractor_2_out_11, n4_bit_subtractor_2_out_12, n4_bit_subtractor_2_out_14,
       n4_bit_subtractor_3_out_10, n4_bit_subtractor_3_out_11, n4_bit_subtractor_3_out_12,
       n4_bit_subtractor_3_out_14, n4_bit_subtractor_4_out_14;

  _4_Bit_Subtractor u_4_bit_subtractor_1 (
    .A0(A[3]), .B0(B[0]), .A1(1'b0), .B1(B[1]), .A2(1'b0), .B2(B[2]), .A3(1'b0), .B3(B[3]), .CP(1'b0),
    .out_10(n4_bit_subtractor_1_out_10), .out_11(n4_bit_subtractor_1_out_11),
    .out_12(n4_bit_subtractor_1_out_12), .out_13(n4_bit_subtractor_1_out_13),
    .out_14(n4_bit_subtractor_1_out_14));
  Multiplexer #(.enable("false")) multiplexer_1 (
    .in0(n4_bit_subtractor_1_out_10), .in1(A[3]), .out(multiplexer_1_out), .sel(n4_bit_subtractor_1_out_14));
  Multiplexer #(.enable("false")) multiplexer_2 (
    .in0(n4_bit_subtractor_1_out_11), .in1(1'b0), .out(multiplexer_2_out), .sel(n4_bit_subtractor_1_out_14));
  Multiplexer #(.enable("false")) multiplexer_3 (
    .in0(n4_bit_subtractor_1_out_12), .in1(1'b0), .out(multiplexer_3_out), .sel(n4_bit_subtractor_1_out_14));
  _4_Bit_Subtractor u_4_bit_subtractor_2 (
    .A0(A[2]), .B0(B[0]), .A1(multiplexer_1_out), .B1(B[1]), .A2(multiplexer_2_out), .B2(B[2]),
    .A3(multiplexer_3_out), .B3(B[3]), .CP(1'b0), .out_10(n4_bit_subtractor_2_out_10),
    .out_11(n4_bit_subtractor_2_out_11), .out_12(n4_bit_subtractor_2_out_12),
    .out_13(n4_bit_subtractor_1_out_13), .out_14(n4_bit_subtractor_2_out_14));
  Multiplexer #(.enable("false")) multiplexer_4 (
    .in0(n4_bit_subtractor_2_out_10), .in1(A[2]), .out(multiplexer_4_out), .sel(n4_bit_subtractor_2_out_14));
  Multiplexer #(.enable("false")) multiplexer_5 (
    .in0(n4_bit_subtractor_2_out_11), .in1(multiplexer_1_out), .out(multiplexer_5_out),
    .sel(n4_bit_subtractor_2_out_14));
  Multiplexer #(.enable("false")) multiplexer_6 (
    .in0(n4_bit_subtractor_2_out_12), .in1(multiplexer_2_out), .out(multiplexer_6_out),
    .sel(n4_bit_subtractor_2_out_14));
  _4_Bit_Subtractor u_4_bit_subtractor_3 (
    .A0(A[1]), .B0(B[0]), .A1(multiplexer_4_out), .B1(B[1]), .A2(multiplexer_5_out), .B2(B[2]),
    .A3(multiplexer_6_out), .B3(B[3]), .CP(1'b0), .out_10(n4_bit_subtractor_3_out_10),
    .out_11(n4_bit_subtractor_3_out_11), .out_12(n4_bit_subtractor_3_out_12),
    .out_13(n4_bit_subtractor_1_out_13), .out_14(n4_bit_subtractor_3_out_14));
  Multiplexer #(.enable("false")) multiplexer_7 (
    .in0(n4_bit_subtractor_3_out_10), .in1(A[1]), .out(multiplexer_7_out), .sel(n4_bit_subtractor_3_out_14));
  Multiplexer #(.enable("false")) multiplexer_8 (
    .in0(n4_bit_subtractor_3_out_11), .in1(multiplexer_4_out), .out(multiplexer_8_out),
    .sel(n4_bit_subtractor_3_out_14));
  Multiplexer #(.enable("false")) multiplexer_9 (
    .in0(n4_bit_subtractor_3_out_12), .in1(multiplexer_5_out), .out(multiplexer_9_out),
    .sel(n4_bit_subtractor_3_out_14));
  _4_Bit_Subtractor u_4_bit_subtractor_4 (
    .A0(A[0]), .B0(B[0]), .A1(multiplexer_7_out), .B1(B[1]), .A2(multiplexer_8_out), .B2(B[2]),
    .A3(multiplexer_9_out), .B3(B[3]), .CP(1'b0), .out_10(n4_bit_subtractor_1_out_13),
    .out_11(n4_bit_subtractor_1_out_13), .out_12(n4_bit_subtractor_1_out_13),
    .out_13(n4_bit_subtractor_1_out_13), .out_14(n4_bit_subtractor_4_out_14));
  not not_1 (Result[3], n4_bit_subtractor_1_out_14);
  xor xor_1 (SIGN, A[4], B[4]);
  not not_2 (Result[0], n4_bit_subtractor_4_out_14);
  not not_3 (Result[1], n4_bit_subtractor_3_out_14);
  not not_4 (Result[2], n4_bit_subtractor_2_out_14);

  assign Result[7:4] = 4'b0000;
  // also tied to GND on the sheet: n4_bit_subtractor_1_out_13

  // Notes on the sheet:
  //   0
  //   0
  //   Q3
  //   Q2
  //   Q1
endmodule

module Binary_To_BCD_4_Bits (
  input  A3,
  input  A2,
  input  A1,
  input  A0,
  output S3,
  output S2,
  output S1,
  output S0
);

  wire A1A0_out, A1A2_out, A2A0_out, A2A1_A0_out, A2A1_out, A2A1A0_out, A3_A2_A0_out, A3A0_2_out, A3A0_out,
       and_1_out, and_2_out, and_3_out, not_1_out, not_2_out, not_3_out, not_4_out, or_1_out, or_4_out,
       or_6_out;

  not not_1 (not_1_out, A2);
  not not_2 (not_2_out, A1);
  not not_3 (not_3_out, A0);
  not not_4 (not_4_out, A3);
  and A2A0 (A2A0_out, A2, A0);
  and A2A1 (A2A1_out, A2, A1);
  and A3A0 (A3A0_out, A3, A0);
  and and_1 (and_1_out, A2, not_2_out);
  and A1A0 (A1A0_out, A1, A0);
  and A1A2 (A1A2_out, A1, not_1_out);
  and A3A0_2 (A3A0_2_out, A3, not_3_out);
  and and_2 (and_2_out, not_4_out, not_1_out);
  and and_3 (and_3_out, A2, A1);
  and A2A1_A0 (A2A1_A0_out, and_1_out, not_3_out);
  and A3_A2_A0 (A3_A2_A0_out, and_2_out, A0);
  and A2A1A0 (A2A1A0_out, and_3_out, not_3_out);
  or or_1 (or_1_out, A3, A2A0_out);
  or or_2 (S3, or_1_out, A2A1_out);
  or or_3 (S2, A3A0_out, A2A1_A0_out);
  or or_4 (or_4_out, A1A0_out, A1A2_out);
  or or_5 (S1, or_4_out, A3A0_2_out);
  or or_6 (or_6_out, A3A0_2_out, A3_A2_A0_out);
  or or_7 (S0, or_6_out, A2A1A0_out);
endmodule

module Binary_To_BCD_8_Bits (
  input  [7:0] A,
  output out_2,
  output out_3,
  output out_4,
  output out_5,
  output out_6,
  output out_7,
  output out_8,
  output out_9,
  output out_10,
  output out_11,
  output out_12,
  output out_13
);

  wire binary_to_bcd_4_bits_1_s0, binary_to_bcd_4_bits_1_s1, binary_to_bcd_4_bits_1_s2, C1_s0, C1_s1, C1_s2,
       C1_s3, C2_s0, C2_s1, C2_s2, C2_s3, C3_s0, C3_s1, C3_s2, C3_s3, C4_s0, C4_s1, C4_s2, C4_s3;

  Binary_To_BCD_4_Bits C1 (.A3(1'b0), .A2(A[7]), .A1(A[6]), .A0(A[5]), .S3(C1_s3), .S2(C1_s2), .S1(C1_s1), .S0(C1_s0));
  Binary_To_BCD_4_Bits C2 (
    .A3(C1_s2), .A2(C1_s1), .A1(C1_s0), .A0(A[4]), .S3(C2_s3), .S2(C2_s2), .S1(C2_s1), .S0(C2_s0));
  Binary_To_BCD_4_Bits C3 (
    .A3(C2_s2), .A2(C2_s1), .A1(C2_s0), .A0(A[3]), .S3(C3_s3), .S2(C3_s2), .S1(C3_s1), .S0(C3_s0));
  Binary_To_BCD_4_Bits C4 (
    .A3(C3_s2), .A2(C3_s1), .A1(C3_s0), .A0(A[2]), .S3(C4_s3), .S2(C4_s2), .S1(C4_s1), .S0(C4_s0));
  Binary_To_BCD_4_Bits C5 (
    .A3(C4_s2), .A2(C4_s1), .A1(C4_s0), .A0(A[1]), .S3(out_9), .S2(out_10), .S1(out_11), .S0(out_12));
  Binary_To_BCD_4_Bits binary_to_bcd_4_bits_1 (
    .A3(1'b0), .A2(C1_s3), .A1(C2_s3), .A0(C3_s3), .S3(out_4), .S2(binary_to_bcd_4_bits_1_s2),
    .S1(binary_to_bcd_4_bits_1_s1), .S0(binary_to_bcd_4_bits_1_s0));
  Binary_To_BCD_4_Bits binary_to_bcd_4_bits_2 (
    .A3(binary_to_bcd_4_bits_1_s2), .A2(binary_to_bcd_4_bits_1_s1), .A1(binary_to_bcd_4_bits_1_s0),
    .A0(C4_s3), .S3(out_5), .S2(out_6), .S1(out_7), .S0(out_8));

  assign out_2 = 1'b0;
  assign out_3 = 1'b0;
  assign out_13 = A[0];

  // Notes on the sheet:
  //   Ground(0)
  //   Last Two Pins (Always (0)) Just because we need 12 Output Bit 
  //   K4
  //   K3
  //   K2
  //   K1
  //   V4
  //   V3
  //   V2
  //   V1
  //   W4
  //   W3
  //   W2
  //   W1
  //   S4
  //   S3
  //   S2
  //   S1
  //   P4
  //   P3
  //   P2
  //   P1
  //   P0
  //   P9
  //   P8
  //   P7
  //   P6
  //   P5
endmodule

module BCD_To_7_Segments (
  input  A,
  input  B,
  input  C,
  input  D,
  output a_2,
  output b_2,
  output c_2,
  output d_2,
  output e,
  output f,
  output g
);

  wire and_1_out, and_2_out, and_3_out, and_4_out, and_5_out, and_6_out, and_7_out, and_8_out, and_9_out,
       and_10_out, and_11_out, not_1_out, not_2_out, not_3_out, or_1_out, or_2_out, or_3_out, or_4_out,
       or_5_out, or_6_out, or_7_out, or_8_out, or_10_out, or_11_out, or_12_out, or_13_out;

  not not_1 (not_1_out, B);
  not not_2 (not_2_out, C);
  not not_3 (not_3_out, D);
  and and_1 (and_1_out, B, D);
  and and_2 (and_2_out, not_1_out, not_3_out);
  and and_3 (and_3_out, B, D);
  and and_4 (and_4_out, C, D);
  and and_5 (and_5_out, not_2_out, not_3_out);
  and and_6 (and_6_out, C, not_3_out);
  and and_7 (and_7_out, not_1_out, C);
  and and_8 (and_8_out, and_1_out, not_2_out);
  and and_9 (and_9_out, A, not_2_out);
  and and_10 (and_10_out, B, not_2_out);
  and and_11 (and_11_out, B, not_3_out);
  or or_1 (or_1_out, B, D);
  or or_2 (or_2_out, C, A);
  or or_3 (or_3_out, and_2_out, and_3_out);
  or or_4 (or_4_out, A, not_1_out);
  or or_5 (or_5_out, and_4_out, and_5_out);
  or or_6 (or_6_out, A, and_2_out);
  or or_7 (or_7_out, or_6_out, or_8_out);
  or or_8 (or_8_out, and_6_out, and_7_out);
  or or_9 (e, and_6_out, and_2_out);
  or or_10 (or_10_out, and_5_out, and_9_out);
  or or_11 (or_11_out, and_10_out, and_11_out);
  or or_12 (or_12_out, and_6_out, and_7_out);
  or or_13 (or_13_out, and_10_out, and_9_out);
  or or_14 (a_2, or_2_out, or_3_out);
  or or_15 (b_2, or_4_out, or_5_out);
  or or_16 (c_2, or_1_out, not_2_out);
  or or_17 (d_2, or_7_out, and_8_out);
  or or_18 (f, or_10_out, or_11_out);
  or or_19 (g, or_12_out, or_13_out);
endmodule

module Full_Binary_to_BCD____7Segment_Together (
  input  [7:0] A,
  output out_2,
  output out_3,
  output out_4,
  output out_5,
  output out_6,
  output out_7,
  output out_8,
  output out_9,
  output out_10,
  output out_11,
  output out_12,
  output out_13,
  output out_14,
  output out_15,
  output out_16,
  output out_17,
  output out_18,
  output out_19,
  output out_20,
  output out_21,
  output out_22
);

  wire binary_to_bcd_8_bits_1_out_2, binary_to_bcd_8_bits_1_out_3, binary_to_bcd_8_bits_1_out_4,
       binary_to_bcd_8_bits_1_out_5, binary_to_bcd_8_bits_1_out_6, binary_to_bcd_8_bits_1_out_7,
       binary_to_bcd_8_bits_1_out_8, binary_to_bcd_8_bits_1_out_9, binary_to_bcd_8_bits_1_out_10,
       binary_to_bcd_8_bits_1_out_11, binary_to_bcd_8_bits_1_out_12, binary_to_bcd_8_bits_1_out_13;

  Binary_To_BCD_8_Bits binary_to_bcd_8_bits_1 (
    .A(A), .out_2(binary_to_bcd_8_bits_1_out_2), .out_3(binary_to_bcd_8_bits_1_out_3),
    .out_4(binary_to_bcd_8_bits_1_out_4), .out_5(binary_to_bcd_8_bits_1_out_5),
    .out_6(binary_to_bcd_8_bits_1_out_6), .out_7(binary_to_bcd_8_bits_1_out_7),
    .out_8(binary_to_bcd_8_bits_1_out_8), .out_9(binary_to_bcd_8_bits_1_out_9),
    .out_10(binary_to_bcd_8_bits_1_out_10), .out_11(binary_to_bcd_8_bits_1_out_11),
    .out_12(binary_to_bcd_8_bits_1_out_12), .out_13(binary_to_bcd_8_bits_1_out_13));
  BCD_To_7_Segments bcd_to_7_segments_1 (
    .A(binary_to_bcd_8_bits_1_out_2), .B(binary_to_bcd_8_bits_1_out_3), .C(binary_to_bcd_8_bits_1_out_4),
    .D(binary_to_bcd_8_bits_1_out_5), .a_2(out_2), .b_2(out_3), .c_2(out_4), .d_2(out_5), .e(out_6),
    .f(out_7), .g(out_8));
  BCD_To_7_Segments bcd_to_7_segments_2 (
    .A(binary_to_bcd_8_bits_1_out_6), .B(binary_to_bcd_8_bits_1_out_7), .C(binary_to_bcd_8_bits_1_out_8),
    .D(binary_to_bcd_8_bits_1_out_9), .a_2(out_9), .b_2(out_10), .c_2(out_11), .d_2(out_12), .e(out_13),
    .f(out_14), .g(out_15));
  BCD_To_7_Segments bcd_to_7_segments_3 (
    .A(binary_to_bcd_8_bits_1_out_10), .B(binary_to_bcd_8_bits_1_out_11), .C(binary_to_bcd_8_bits_1_out_12),
    .D(binary_to_bcd_8_bits_1_out_13), .a_2(out_16), .b_2(out_17), .c_2(out_18), .d_2(out_19), .e(out_20),
    .f(out_21), .g(out_22));

  // Notes on the sheet:
  //   a
  //   b
  //   c
  //   d
  //   e
  //   f
  //   g
  //   a
  //   b
  //   c
  //   d
  //   e
  //   f
  //   g
  //   a
  //   b
  //   c
  //   d
  //   e
  //   f
  //   g
endmodule

module Main_Interface (
  input  [4:0] A,
  input  [1:0] Select_Operation,
  input  [4:0] B
);

  wire and_1_out, and_2_out, and_3_out, final_adder_1_sign_output, final_division_1_sign,
       final_multiplication_1_c8_sign, final_subtraction_1_sign_output,
       full_binary_to_bcd_7segment_together_1_out_2, full_binary_to_bcd_7segment_together_1_out_3,
       full_binary_to_bcd_7segment_together_1_out_4, full_binary_to_bcd_7segment_together_1_out_5,
       full_binary_to_bcd_7segment_together_1_out_6, full_binary_to_bcd_7segment_together_1_out_7,
       full_binary_to_bcd_7segment_together_1_out_8, full_binary_to_bcd_7segment_together_1_out_9,
       full_binary_to_bcd_7segment_together_1_out_10, full_binary_to_bcd_7segment_together_1_out_11,
       full_binary_to_bcd_7segment_together_1_out_12, full_binary_to_bcd_7segment_together_1_out_13,
       full_binary_to_bcd_7segment_together_1_out_14, full_binary_to_bcd_7segment_together_1_out_15,
       full_binary_to_bcd_7segment_together_1_out_16, full_binary_to_bcd_7segment_together_1_out_17,
       full_binary_to_bcd_7segment_together_1_out_18, full_binary_to_bcd_7segment_together_1_out_19,
       full_binary_to_bcd_7segment_together_1_out_20, full_binary_to_bcd_7segment_together_1_out_21,
       full_binary_to_bcd_7segment_together_1_out_22, multiplexer_2_out;
  wire [7:0] final_adder_1_result, final_division_1_result, final_multiplication_1_result,
       final_subtraction_1_result, multiplexer_1_out, multiplexer_3_out;

  Final_Adder_2 final_adder_1 (.A(A), .B(B), .Result(final_adder_1_result), .Sign_Output(final_adder_1_sign_output));
  Final_Subtraction final_subtraction_1 (
    .A(A), .B(B), .Result(final_subtraction_1_result), .Sign_Output(final_subtraction_1_sign_output));
  Final_Multiplication final_multiplication_1 (
    .A(A), .B(B), .Result(final_multiplication_1_result), .C8_SIGN(final_multiplication_1_c8_sign));
  Final_Division final_division_1 (.A(A), .B(B), .Result(final_division_1_result), .SIGN(final_division_1_sign));
  Full_Binary_to_BCD____7Segment_Together full_binary_to_bcd_7segment_together_1 (
    .A(multiplexer_1_out), .out_2(full_binary_to_bcd_7segment_together_1_out_2),
    .out_3(full_binary_to_bcd_7segment_together_1_out_3),
    .out_4(full_binary_to_bcd_7segment_together_1_out_4),
    .out_5(full_binary_to_bcd_7segment_together_1_out_5),
    .out_6(full_binary_to_bcd_7segment_together_1_out_6),
    .out_7(full_binary_to_bcd_7segment_together_1_out_7),
    .out_8(full_binary_to_bcd_7segment_together_1_out_8),
    .out_9(full_binary_to_bcd_7segment_together_1_out_9),
    .out_10(full_binary_to_bcd_7segment_together_1_out_10),
    .out_11(full_binary_to_bcd_7segment_together_1_out_11),
    .out_12(full_binary_to_bcd_7segment_together_1_out_12),
    .out_13(full_binary_to_bcd_7segment_together_1_out_13),
    .out_14(full_binary_to_bcd_7segment_together_1_out_14),
    .out_15(full_binary_to_bcd_7segment_together_1_out_15),
    .out_16(full_binary_to_bcd_7segment_together_1_out_16),
    .out_17(full_binary_to_bcd_7segment_together_1_out_17),
    .out_18(full_binary_to_bcd_7segment_together_1_out_18),
    .out_19(full_binary_to_bcd_7segment_together_1_out_19),
    .out_20(full_binary_to_bcd_7segment_together_1_out_20),
    .out_21(full_binary_to_bcd_7segment_together_1_out_21),
    .out_22(full_binary_to_bcd_7segment_together_1_out_22));
  Multiplexer #(.select(2), .width(8), .enable("false")) multiplexer_1 (
    .in0(final_adder_1_result), .in1(final_subtraction_1_result), .in2(final_multiplication_1_result),
    .in3(final_division_1_result), .out(multiplexer_1_out), .sel(Select_Operation));
  Multiplexer #(.select(2), .enable("false")) multiplexer_2 (
    .in0(final_adder_1_sign_output), .in1(final_subtraction_1_sign_output),
    .in2(final_multiplication_1_c8_sign), .in3(final_division_1_sign), .out(multiplexer_2_out),
    .sel(Select_Operation));
  Multiplexer #(.select(2), .width(8), .enable("false")) multiplexer_3 (
    .in3(final_division_1_result), .out(multiplexer_3_out), .sel(Select_Operation));  // open: in0, in1, in2
  and and_1 (and_1_out, multiplexer_3_out[3], multiplexer_3_out[2]);
  and and_2 (and_2_out, multiplexer_3_out[1], multiplexer_3_out[0]);
  and and_3 (and_3_out, and_1_out, and_2_out);
  LED Divsion_By_ZeroFlag (.in(and_3_out));
  LED Sign_Flag (.in(multiplexer_2_out));
  _7_Segment_Display u_7_segment_display_1 (
    .g(full_binary_to_bcd_7segment_together_1_out_8), .f(full_binary_to_bcd_7segment_together_1_out_7),
    .a(full_binary_to_bcd_7segment_together_1_out_2), .b(full_binary_to_bcd_7segment_together_1_out_3),
    .e(full_binary_to_bcd_7segment_together_1_out_6), .d(full_binary_to_bcd_7segment_together_1_out_5),
    .c(full_binary_to_bcd_7segment_together_1_out_4));  // open: dp
  _7_Segment_Display u_7_segment_display_2 (
    .g(full_binary_to_bcd_7segment_together_1_out_15), .f(full_binary_to_bcd_7segment_together_1_out_14),
    .a(full_binary_to_bcd_7segment_together_1_out_9), .b(full_binary_to_bcd_7segment_together_1_out_10),
    .e(full_binary_to_bcd_7segment_together_1_out_13), .d(full_binary_to_bcd_7segment_together_1_out_12),
    .c(full_binary_to_bcd_7segment_together_1_out_11));  // open: dp
  _7_Segment_Display u_7_segment_display_3 (
    .g(full_binary_to_bcd_7segment_together_1_out_22), .f(full_binary_to_bcd_7segment_together_1_out_21),
    .a(full_binary_to_bcd_7segment_together_1_out_16), .b(full_binary_to_bcd_7segment_together_1_out_17),
    .e(full_binary_to_bcd_7segment_together_1_out_20), .d(full_binary_to_bcd_7segment_together_1_out_19),
    .c(full_binary_to_bcd_7segment_together_1_out_18));  // open: dp
endmodule
