// Logisim project New.circ as structural Verilog
module Half_Adder (
  input  A0,
  input  B0,
  output S0,
  output C0
);

  xor xor_1 (S0, A0, B0);
  and and_1 (C0, A0, B0);
endmodule

module _1_Bit_Comparator_for_Sign (
  input  A0,
  input  B0,
  input  SIGN_A,
  input  SIGN_B,
  output Sign
);

  wire A0As_out, A0AsB0_prime_out, A0AsB0Bs_out, B0Bs_out, BoBsAo_prime_out, not_1_out, not_2_out, or_1_out;

  not not_1 (not_1_out, A0);
  not not_2 (not_2_out, B0);
  and A0As (A0As_out, A0, SIGN_A);
  and B0Bs (B0Bs_out, B0, SIGN_B);
  and A0AsB0Bs (A0AsB0Bs_out, A0As_out, B0Bs_out);
  and BoBsAo_prime (BoBsAo_prime_out, B0Bs_out, not_1_out);
  and A0AsB0_prime (A0AsB0_prime_out, A0As_out, not_2_out);
  or or_1 (or_1_out, A0AsB0Bs_out, BoBsAo_prime_out);
  or or_2 (Sign, or_1_out, A0AsB0_prime_out);
endmodule

module _2_Bit_Adder_with_Sign (
  input  A0,
  input  B0,
  input  SIGN_A,
  input  SIGN_B,
  input  Cin_prime,
  output Sum,
  output Carry,
  output Sign
);

  wire and_2_out, half_adder_1_c0, half_adder_1_s0, n1_bit_comparator_for_sign_1_sign, not_1_out, xnor_1_out;

  xnor xnor_1 (xnor_1_out, SIGN_A, SIGN_B);
  not not_1 (not_1_out, Cin_prime);
  Half_Adder half_adder_1 (.A0(A0), .B0(B0), .S0(half_adder_1_s0), .C0(half_adder_1_c0));
  _1_Bit_Comparator_for_Sign u_1_bit_comparator_for_sign_1 (
    .A0(A0), .B0(B0), .Sign(n1_bit_comparator_for_sign_1_sign), .SIGN_A(SIGN_A), .SIGN_B(SIGN_B));
  and and_1 (Sum, half_adder_1_s0, not_1_out);
  and and_2 (and_2_out, half_adder_1_c0, xnor_1_out);
  and and_3 (Sign, n1_bit_comparator_for_sign_1_sign, not_1_out);
  and and_4 (Carry, and_2_out, not_1_out);
endmodule

module Half_Sub (
  input  in_1,
  input  in_2,
  input  in_3,
  input  in_4,
  input  in_5,
  input  in_6,
  input  in_7,
  input  in_8,
  input  in_9,
  input  in_10
);
endmodule
