// Logisim project sub.circ as structural Verilog
module _4_Bit_Sub (
  input  A0,
  input  B0,
  input  A1,
  input  B1,
  input  A2,
  input  B2,
  input  A3,
  input  B3,
  input  CP,
  output out_10,
  output out_11,
  output out_12,
  output out_13
);

  wire full_subtractor_1_c, full_subtractor_2_c, full_subtractor_3_c, full_subtractor_4_c;

  Full_Subtractor full_subtractor_1 (.A(A0), .B(B0), .cp(CP), .S(out_10), .C(full_subtractor_1_c));
  Full_Subtractor full_subtractor_2 (.A(A1), .B(B1), .cp(full_subtractor_1_c), .S(out_11), .C(full_subtractor_2_c));
  Full_Subtractor full_subtractor_3 (.A(A2), .B(B2), .cp(full_subtractor_2_c), .S(out_12), .C(full_subtractor_3_c));
  Full_Subtractor full_subtractor_4 (.A(A3), .B(B3), .cp(full_subtractor_3_c), .S(out_13), .C(full_subtractor_4_c));
  // also tied to GND on the sheet: full_subtractor_4_c
endmodule

module Full_Subtractor (
  input  A,
  input  B,
  input  cp,
  output S,
  output C
);

  wire and_1_out, and_2_out, and_3_out, not_1_out;

  not not_1 (not_1_out, A);
  xor xor_1 (S, A, B, cp);
  and and_1 (and_1_out, not_1_out, B);
  and and_2 (and_2_out, not_1_out, cp);
  and and_3 (and_3_out, B, cp);
  or or_1 (C, and_1_out, and_2_out, and_3_out);
endmodule
